// Digital circuit Cpu.dig as structural Verilog
module Cpu (
  input  Clock
);

  wire ArithCarry, CarrySelectA, CarrySelectADelayed, CarrySelectB, CarrySelectBDelayed,
       Control__ALU__Assert, Control__DI__AssertAddr, Control__DI__AssertXfer, Control__DI__Dec,
       Control__DI__Inc, Control__DI__LoadXfer, Control__MemBridge__Assert, Control__MemBridge__Direction,
       Control__MemBridge__Load, Control__PCRA0__AssertAddr, Control__PCRA0__AssertXfer, Control__PCRA0__Dec,
       Control__PCRA0__Inc, Control__PCRA0__LoadXfer, Control__PCRA1__AssertAddr, Control__PCRA1__AssertXfer,
       Control__PCRA1__Dec, Control__PCRA1__Inc, Control__PCRA1__LoadXfer, Control__Reg__A__Assert,
       Control__Reg__A__LHS, Control__Reg__A__Load, Control__Reg__A__RHS, Control__Reg__B__Assert,
       Control__Reg__B__LHS, Control__Reg__B__Load, Control__Reg__B__RHS, Control__Reg__C__Assert,
       Control__Reg__C__LHS, Control__Reg__C__Load, Control__Reg__C__RHS, Control__Reg__Const__Assert,
       Control__Reg__Const__Load, Control__Reg__D__Assert, Control__Reg__D__LHS, Control__Reg__D__Load,
       Control__Reg__D__RHS, Control__Reg__TH__Assert, Control__Reg__TH__Load, Control__Reg__TL__Assert,
       Control__Reg__TL__Load, Control__SI__AssertAddr, Control__SI__AssertXfer, Control__SI__Dec,
       Control__SI__Inc, Control__SI__LoadXfer, Control__SP__AssertAddr, Control__SP__AssertXfer,
       Control__SP__Dec, Control__SP__Inc, Control__SP__LoadXfer, Control__TX__AssertAddr,
       Control__TX__AssertMode, Control__TX__AssertXfer, Control__TX__LoadXfer, Flags__0__Overflow,
       Flags__1__Sign, Flags__2__Zero, Flags__3__CarryA, Flags__4__CarryL, Flags__5__PCRA__Flip,
       Flags__6__Reset, Pipe0Out__0__Inc__PCRA0, Pipe0Out__1__Inc__PCRA1, Pipe1Out__0__LHS0,
       Pipe1Out__1__LHS1, Pipe1Out__2__RHS0, Pipe1Out__3__RHS1, Pipe1Out__4__ALUOP0, Pipe1Out__5__ALUOP1,
       Pipe1Out__6__ALUOP2, Pipe1Out__7__ALUOP3, Pipe1Out__8__Xfer__LoadDec0, Pipe1Out__9__Xfer__LoadDec1,
       Pipe1Out__10__Xfer__LoadDec2, Pipe1Out__11__Xfer__LoadDec3, Pipe1Out__12__Xfer__Assert0,
       Pipe1Out__13__Xfer__Assert1, Pipe1Out__14__Xfer__Assert2, Pipe1Out__15__FetchSuppress,
       Pipe2Out__0__MainBus__Assert0, Pipe2Out__1__MainBus__Assert1, Pipe2Out__2__MainBus__Assert2,
       Pipe2Out__3__MainBus__Assert3, Pipe2Out__4__MainBus__Load0, Pipe2Out__5__MainBus__Load1,
       Pipe2Out__6__MainBus__Load2, Pipe2Out__7__MainBus__Load3, Pipe2Out__8__Inc__SPSIDI0,
       Pipe2Out__9__Inc__SPSIDI1, Pipe2Out__10__AddrSel0, Pipe2Out__11__AddrSel1, Pipe2Out__12__AddrSel2,
       Pipe2Out__13__BusRequest, Pipe2Out__15__Break, ResetIn, Shift__CarryOut, ShiftSelectA, ShiftSelectB;
  wire [3:0] LogicSelect;
  wire [7:0] A_registercontents, B_registercontents, Bus__LHS, Bus__Main, BUS__Memory, Bus__RHS,
       C_registercontents, D_registercontents, Data, Logic__RHSOut, Pipe0Out__Pipeline, Pipe1Out__Pipeline,
       Pipe2Out__Pipeline, Shift__LHSOut;
  wire [15:0] BUS__Addr, BUS__Xfer, DI_reg__contents, PCRA0_reg__contents, PCRA1_reg__contents,
       reg_16bit_xfer_1_register__value, SI_reg__contents, Stack_Pointer_reg__contents;

  reg_16bit_updownload PCRA0 (
    .Clock(Clock), .Clear(Flags__6__Reset), .nAssertAddr(Control__PCRA0__AssertAddr),
    .nAssertBus(Control__PCRA0__AssertXfer), .nLoad(Control__PCRA0__LoadXfer), .Inc(Control__PCRA0__Inc),
    .Dec(Control__PCRA0__Dec), .Addr(BUS__Addr), .Bus(BUS__Xfer), .Reg__Contents(PCRA0_reg__contents));  // open: nCarry, nBorrow
  reg_16bit_updownload PCRA1 (
    .Clock(Clock), .Clear(Flags__6__Reset), .nAssertAddr(Control__PCRA1__AssertAddr),
    .nAssertBus(Control__PCRA1__AssertXfer), .nLoad(Control__PCRA1__LoadXfer), .Inc(Control__PCRA1__Inc),
    .Dec(Control__PCRA1__Dec), .Addr(BUS__Addr), .Bus(BUS__Xfer), .Reg__Contents(PCRA1_reg__contents));  // open: nCarry, nBorrow
  reg_16bit_updownload Stack_Pointer (
    .Clock(Clock), .Clear(Flags__6__Reset), .nAssertAddr(Control__SP__AssertAddr),
    .nAssertBus(Control__SP__AssertXfer), .nLoad(Control__SP__LoadXfer), .Inc(Control__SP__Inc),
    .Dec(Control__SP__Dec), .Addr(BUS__Addr), .Bus(BUS__Xfer), .Reg__Contents(Stack_Pointer_reg__contents));  // open: nCarry, nBorrow
  reg_16bit_updownload SI (
    .Clock(Clock), .Clear(Flags__6__Reset), .nAssertAddr(Control__SI__AssertAddr),
    .nAssertBus(Control__SI__AssertXfer), .nLoad(Control__SI__LoadXfer), .Inc(Control__SI__Inc),
    .Dec(Control__SI__Dec), .Addr(BUS__Addr), .Bus(BUS__Xfer), .Reg__Contents(SI_reg__contents));  // open: nCarry, nBorrow
  reg_16bit_updownload DI (
    .Clock(Clock), .Clear(Flags__6__Reset), .nAssertAddr(Control__DI__AssertAddr),
    .nAssertBus(Control__DI__AssertXfer), .nLoad(Control__DI__LoadXfer), .Inc(Control__DI__Inc),
    .Dec(Control__DI__Dec), .Addr(BUS__Addr), .Bus(BUS__Xfer), .Reg__Contents(DI_reg__contents));  // open: nCarry, nBorrow
  reg_16bit_xfer reg_16bit_xfer_1 (
    .Clock(Clock), .Bus__Main(Bus__Main), .Bus__Xfer(BUS__Xfer), .Bus__Addr(BUS__Addr),
    .nAssertMainBusLow(Control__Reg__TL__Assert), .nAssertMainBusHigh(Control__Reg__TH__Assert),
    .nAssertXferBus(Control__TX__AssertXfer), .nAssertAddrBus(Control__TX__AssertAddr),
    .nLoadMainBusLow(Control__Reg__TL__Load), .nLoadMainBusHigh(Control__Reg__TH__Load),
    .nLoadXferBus(Control__TX__LoadXfer), .Register__Value(reg_16bit_xfer_1_register__value));
  // Probe Register\_PCRA0 on PCRA0_reg__contents
  // Probe Register\_PCRA1 on PCRA1_reg__contents
  // Probe Register\_SP on Stack_Pointer_reg__contents
  // Probe Register\_SI on SI_reg__contents
  // Probe Register\_DI on DI_reg__contents
  // Probe Register\_TX on reg_16bit_xfer_1_register__value
  flags Flags (
    .ClockIn(Clock), .ArithCarryIn(ArithCarry), .DataIn(Data), .LogicCarryIn(Shift__CarryOut),
    .LHS(Bus__LHS), .RHS(Bus__RHS), .CarrySelectA(CarrySelectA), .CarrySelectB(CarrySelectB),
    .ArithCarryFlag(Flags__3__CarryA), .ZeroFlag(Flags__2__Zero), .LogicCarryFlag(Flags__4__CarryL),
    .SignFlag(Flags__1__Sign), .OverflowFlag(Flags__0__Overflow), .CarrySelectADelayed(CarrySelectADelayed),
    .CarrySelectBDelayed(CarrySelectBDelayed));
  reg_8bit_generalpurpose A (
    .MainBusIn(Bus__Main), .Reg__Assert__RHS(Control__Reg__A__RHS), .Reg__Assert__LHS(Control__Reg__A__LHS),
    .Reg__Assert(Control__Reg__A__Assert), .Reg__Load(Control__Reg__A__Load), .MainBusOut(Bus__Main),
    .LHSBus(Bus__LHS), .RHSBus(Bus__RHS), .RegisterContents(A_registercontents));
  reg_8bit_generalpurpose B (
    .MainBusIn(Bus__Main), .Reg__Assert__RHS(Control__Reg__B__RHS), .Reg__Assert__LHS(Control__Reg__B__LHS),
    .Reg__Assert(Control__Reg__B__Assert), .Reg__Load(Control__Reg__B__Load), .MainBusOut(Bus__Main),
    .LHSBus(Bus__LHS), .RHSBus(Bus__RHS), .RegisterContents(B_registercontents));
  reg_8bit_generalpurpose C (
    .MainBusIn(Bus__Main), .Reg__Assert__RHS(Control__Reg__C__RHS), .Reg__Assert__LHS(Control__Reg__C__LHS),
    .Reg__Assert(Control__Reg__C__Assert), .Reg__Load(Control__Reg__C__Load), .MainBusOut(Bus__Main),
    .LHSBus(Bus__LHS), .RHSBus(Bus__RHS), .RegisterContents(C_registercontents));
  reg_8bit_generalpurpose D (
    .MainBusIn(Bus__Main), .Reg__Assert__RHS(Control__Reg__D__RHS), .Reg__Assert__LHS(Control__Reg__D__LHS),
    .Reg__Assert(Control__Reg__D__Assert), .Reg__Load(Control__Reg__D__Load), .MainBusOut(Bus__Main),
    .LHSBus(Bus__LHS), .RHSBus(Bus__RHS), .RegisterContents(D_registercontents));
  reg_constant reg_constant_1 (
    .MEMDATAIn(BUS__Memory), .Reg__Assert(Control__Reg__Const__Assert),
    .Reg__Load(Control__Reg__Const__Load), .MainBusOut(Bus__Main));
  memory memory_1 (
    .Addr(BUS__Addr), .MainBus(Bus__Main), .MEMDATA(BUS__Memory),
    .MemBridge__Direction(Control__MemBridge__Direction), .MemBridge__Load(Control__MemBridge__Load),
    .MemBridge__Assert(Control__MemBridge__Assert));
  // Probe Register\_A on A_registercontents
  // Probe Register\_B on B_registercontents
  // Probe Register\_C on C_registercontents
  // Probe Register\_D on D_registercontents
  // adder adder_1: pin names not known; wires that end beside it: Clock, Flags__3__CarryA, Shift__LHSOut, Logic__RHSOut, CarrySelectADelayed, CarrySelectBDelayed, Control__ALU__Assert
  shift LHS_Shift (
    .SelectA(ShiftSelectA), .SelectB(ShiftSelectB), .LHSIn(Bus__LHS), .CarryIn(Flags__4__CarryL),
    .Clock(Clock), .CarryOut(Shift__CarryOut), .LHSOut(Shift__LHSOut));
  // Probe AdderOut on Data
  // Probe BUS\_Xfer on BUS__Xfer
  // Probe BUS\_Main on Bus__Main
  clock_reset clock_reset_1 (.ClockIn(Clock), .ResetIn(ResetIn), .nResetOut(Flags__6__Reset));  // open: ResetOut
  // Probe Shift\_LHSOut on Shift__LHSOut
  LookUpTable #(.Bits(8)) Diode_Matrix (
    .in0(Pipe1Out__4__ALUOP0), .in1(Pipe1Out__5__ALUOP1), .in2(Pipe1Out__6__ALUOP2),
    .in3(Pipe1Out__7__ALUOP3), .out({CarrySelectB, CarrySelectA, ShiftSelectB, ShiftSelectA, LogicSelect}));
  Button #(.activeLow("true")) Reset (.out(ResetIn));
  // Probe Pipe2Out on Pipe2Out__Pipeline
  // Probe Pipe1Out on Pipe1Out__Pipeline
  // Probe Pipe0Out on Pipe0Out__Pipeline
  // Probe BUS\_Addr on BUS__Addr
  // Probe BUS\_Memory on BUS__Memory
  // Probe BUS\_LHS on Bus__LHS
  // Probe BUS\_RHS on Bus__RHS
  \logic  RHS_Logic (.Clock(Clock), .LogicSelect(LogicSelect), .RHS(Bus__RHS), .LHS(Bus__LHS), .RHSOut(Logic__RHSOut));
  // Probe Logic\_Select on LogicSelect
  // Probe Logic\_RHSOut on Logic__RHSOut
  pipeline_stage2 Stage_2 (
    .ClockIn(Clock), .Flags__0__Overflow(Flags__0__Overflow), .Flags__1__Sign(Flags__1__Sign),
    .Flags__2__Zero(Flags__2__Zero), .Flags__3__CarryA(Flags__3__CarryA),
    .Flags__4__CarryL(Flags__4__CarryL), .Flags__5__PCRA__Flip(Flags__5__PCRA__Flip),
    .Flags__6__Reset(Flags__6__Reset), .PipeIn(Pipe1Out__Pipeline), .PipeOut(Pipe2Out__Pipeline),
    .Pipe2Out__0__MainAssert0(Pipe2Out__0__MainBus__Assert0),
    .Pipe2Out__1__MainAssert1(Pipe2Out__1__MainBus__Assert1),
    .Pipe2Out__2__MainAssert2(Pipe2Out__2__MainBus__Assert2),
    .Pipe2Out__3__MainAssert3(Pipe2Out__3__MainBus__Assert3),
    .Pipe2Out__4__MainLoad0(Pipe2Out__4__MainBus__Load0),
    .Pipe2Out__5__MainLoad1(Pipe2Out__5__MainBus__Load1),
    .Pipe2Out__6__MainLoad2(Pipe2Out__6__MainBus__Load2),
    .Pipe2Out__7__MainLoad3(Pipe2Out__7__MainBus__Load3), .Pipe2Out__8__Inc0(Pipe2Out__8__Inc__SPSIDI0),
    .Pipe2Out__9__Inc1(Pipe2Out__9__Inc__SPSIDI1), .Pipe2Out__10__Addr0(Pipe2Out__10__AddrSel0),
    .Pipe2Out__11__Addr1(Pipe2Out__11__AddrSel1), .Pipe2Out__12__Addr2(Pipe2Out__12__AddrSel2),
    .Pipe2Out__13__BusRequest(Pipe2Out__13__BusRequest), .Pipe2Out__14__PCRA__Flip(Flags__5__PCRA__Flip),
    .Pipe2Out__15__Break(Pipe2Out__15__Break));
  pipeline_stage1 Stage_1 (
    .ClockIn(Clock), .BusRequest(Pipe2Out__13__BusRequest), .Flags__0__Overflow(Flags__0__Overflow),
    .Flags__1__Sign(Flags__1__Sign), .Flags__2__Zero(Flags__2__Zero), .Flags__3__CarryA(Flags__3__CarryA),
    .Flags__4__CarryL(Flags__4__CarryL), .Flags__5__PCRA__Flip(Flags__5__PCRA__Flip),
    .Flags__6__Reset(Flags__6__Reset), .PipeIn(Pipe0Out__Pipeline), .PipeOut(Pipe1Out__Pipeline),
    .Pipe1Out__0__LHS0(Pipe1Out__0__LHS0), .Pipe1Out__1__LHS1(Pipe1Out__1__LHS1),
    .Pipe1Out__2__RHS0(Pipe1Out__2__RHS0), .Pipe1Out__3__RHS1(Pipe1Out__3__RHS1),
    .Pipe1Out__4__ALUOP0(Pipe1Out__4__ALUOP0), .Pipe1Out__5__ALUOP1(Pipe1Out__5__ALUOP1),
    .Pipe1Out__6__ALUOP2(Pipe1Out__6__ALUOP2), .Pipe1Out__7__ALUOP3(Pipe1Out__7__ALUOP3),
    .Pipe1Out__8__XLD0(Pipe1Out__8__Xfer__LoadDec0), .Pipe1Out__9__XLD1(Pipe1Out__9__Xfer__LoadDec1),
    .Pipe1Out__10__XLD2(Pipe1Out__10__Xfer__LoadDec2), .Pipe1Out__11__XLD3(Pipe1Out__11__Xfer__LoadDec3),
    .Pipe1Out__12__XA0(Pipe1Out__12__Xfer__Assert0), .Pipe1Out__13__XA1(Pipe1Out__13__Xfer__Assert1),
    .Pipe1Out__14__XA2(Pipe1Out__14__Xfer__Assert2), .Pipe1Out__15__FetchSuppress(Pipe1Out__15__FetchSuppress));
  pipeline_stage0 Stage_0 (
    .MEMDATA(BUS__Memory), .BusRequest(Pipe2Out__13__BusRequest),
    .FetchSuppress(Pipe1Out__15__FetchSuppress), .Flags__5__PCRA__Flip(Flags__5__PCRA__Flip),
    .ClockIn(Clock), .Pipe0Out(Pipe0Out__Pipeline), .Pipe0Out__0__IncPCRA0(Pipe0Out__0__Inc__PCRA0),
    .Pipe0Out__1__IncPCRA1(Pipe0Out__1__Inc__PCRA1));
  // Probe Pipe1 on {Pipe1Out__15__FetchSuppress, Pipe1Out__14__Xfer__Assert2, Pipe1Out__13__Xfer__Assert1, Pipe1Out__12__Xfer__Assert0, Pipe1Out__11__Xfer__LoadDec3, Pipe1Out__10__Xfer__LoadDec2, Pipe1Out__9__Xfer__LoadDec1, Pipe1Out__8__Xfer__LoadDec0, Pipe1Out__7__ALUOP3, Pipe1Out__6__ALUOP2, Pipe1Out__5__ALUOP1, Pipe1Out__4__ALUOP0, Pipe1Out__3__RHS1, Pipe1Out__2__RHS0, Pipe1Out__1__LHS1, Pipe1Out__0__LHS0}
  // Probe Pipe2 on {Pipe2Out__15__Break, Flags__5__PCRA__Flip, Pipe2Out__13__BusRequest, Pipe2Out__12__AddrSel2, Pipe2Out__11__AddrSel1, Pipe2Out__10__AddrSel0, Pipe2Out__9__Inc__SPSIDI1, Pipe2Out__8__Inc__SPSIDI0, Pipe2Out__7__MainBus__Load3, Pipe2Out__6__MainBus__Load2, Pipe2Out__5__MainBus__Load1, Pipe2Out__4__MainBus__Load0, Pipe2Out__3__MainBus__Assert3, Pipe2Out__2__MainBus__Assert2, Pipe2Out__1__MainBus__Assert1, Pipe2Out__0__MainBus__Assert0}
  buscontrol Bus_Control (
    .ClockIn(Clock), .ResetIn(Flags__6__Reset), .MainBus__Assert__0(Pipe2Out__0__MainBus__Assert0),
    .MainBus__Assert__1(Pipe2Out__1__MainBus__Assert1), .MainBus__Assert__2(Pipe2Out__2__MainBus__Assert2),
    .MainBus__Assert__3(Pipe2Out__3__MainBus__Assert3), .MainBus__Load__0(Pipe2Out__4__MainBus__Load0),
    .MainBus__Load__1(Pipe2Out__5__MainBus__Load1), .MainBus__Load__2(Pipe2Out__6__MainBus__Load2),
    .MainBus__Load__3(Pipe2Out__7__MainBus__Load3), .Inc__SPSIDI__0(Pipe2Out__8__Inc__SPSIDI0),
    .Inc__SPSIDI__1(Pipe2Out__9__Inc__SPSIDI1), .AddrSel0(Pipe2Out__10__AddrSel0),
    .AddrSel1(Pipe2Out__11__AddrSel1), .AddrSel2(Pipe2Out__12__AddrSel2), .LHS__0(Pipe1Out__0__LHS0),
    .LHS__1(Pipe1Out__1__LHS1), .RHS__0(Pipe1Out__2__RHS0), .RHS__1(Pipe1Out__3__RHS1),
    .Xfer__Assert0(Pipe1Out__12__Xfer__Assert0), .Xfer__Assert1(Pipe1Out__13__Xfer__Assert1),
    .Xfer__Assert2(Pipe1Out__14__Xfer__Assert2), .Xfer__LoadDec0(Pipe1Out__8__Xfer__LoadDec0),
    .Xfer__LoadDec1(Pipe1Out__9__Xfer__LoadDec1), .Xfer__LoadDec2(Pipe1Out__10__Xfer__LoadDec2),
    .Xfer__LoadDec3(Pipe1Out__11__Xfer__LoadDec3), .Inc__PCRA__0(Pipe0Out__0__Inc__PCRA0),
    .Inc__PCRA__1(Pipe0Out__1__Inc__PCRA1), .Reg__A__LHS(Control__Reg__A__LHS),
    .Reg__B__LHS(Control__Reg__B__LHS), .Reg__C__LHS(Control__Reg__C__LHS),
    .Reg__D__LHS(Control__Reg__D__LHS), .Reg__A__RHS(Control__Reg__A__RHS),
    .Reg__B__RHS(Control__Reg__B__RHS), .Reg__C__RHS(Control__Reg__C__RHS),
    .Reg__D__RHS(Control__Reg__D__RHS), .Reg__A__Assert(Control__Reg__A__Assert),
    .Reg__B__Assert(Control__Reg__B__Assert), .Reg__C__Assert(Control__Reg__C__Assert),
    .Reg__D__Assert(Control__Reg__D__Assert), .Reg__Const__Assert(Control__Reg__Const__Assert),
    .Reg__TL__Assert(Control__Reg__TL__Assert), .Reg__TH__Assert(Control__Reg__TH__Assert),
    .Alu__Assert(Control__ALU__Assert), .MemBridge__Assert(Control__MemBridge__Assert),
    .Reg__A__Load(Control__Reg__A__Load), .Reg__B__Load(Control__Reg__B__Load),
    .Reg__C__Load(Control__Reg__C__Load), .Reg__D__Load(Control__Reg__D__Load),
    .Reg__TL__Load(Control__Reg__TL__Load), .Reg__TH__Load(Control__Reg__TH__Load),
    .MemBridge__Load(Control__MemBridge__Load), .MemBridge__Direction(Control__MemBridge__Direction),
    .Reg__PCRA0__Inc(Control__PCRA0__Inc), .Reg__PCRA1__Inc(Control__PCRA1__Inc),
    .Reg__SP__Inc(Control__SP__Inc), .Reg__SI__Inc(Control__SI__Inc), .Reg__DI__Inc(Control__DI__Inc),
    .Reg__PCRA0__AXfer(Control__PCRA0__AssertXfer), .Reg__PCRA1__AXfer(Control__PCRA1__AssertXfer),
    .Reg__SP__AXfer(Control__SP__AssertXfer), .Reg__SI__AXfer(Control__SI__AssertXfer),
    .Reg__DI__AXfer(Control__DI__AssertXfer), .Reg__TX__AXfer(Control__TX__AssertXfer),
    .Reg__TX__AMode(Control__TX__AssertMode), .Reg__PCRA0__LXfer(Control__PCRA0__LoadXfer),
    .Reg__PCRA1__LXfer(Control__PCRA1__LoadXfer), .Reg__SP__LXfer(Control__SP__LoadXfer),
    .Reg__SI__LXfer(Control__SI__LoadXfer), .Reg__DI__LXfer(Control__DI__LoadXfer),
    .Reg__TX__LXfer(Control__TX__LoadXfer), .Reg__Const__LMem(Control__Reg__Const__Load),
    .Reg__PCRA0__Dec(Control__PCRA0__Dec), .Reg__PCRA1__Dec(Control__PCRA1__Dec),
    .Reg__SP__Dec(Control__SP__Dec), .Reg__SI__Dec(Control__SI__Dec), .Reg__DI__Dec(Control__DI__Dec),
    .Reg__PCRA0__AAddr(Control__PCRA0__AssertAddr), .Reg__PCRA1__AAddr(Control__PCRA1__AssertAddr),
    .Reg__SP__AAddr(Control__SP__AssertAddr), .Reg__SI__AAddr(Control__SI__AssertAddr),
    .Reg__DI__AAddr(Control__DI__AssertAddr), .Reg__TX__AAddr(Control__TX__AssertAddr));  // open: Dev9__Assert, Dev10__Assert, Dev11__Assert, Dev12__Assert, Dev13__Assert, Dev14__Assert, Reg__Const__Load, Alu__Load, Dev9__Load, Dev10__Load, Dev11__Load, Dev12__Load, Dev13__Load, Dev14__Load, Memory__Ack

  // Other names for the same wires on the sheet: Pipe2Out__14__PCRA__Flip = Flags__5__PCRA__Flip

  // Notes on the sheet:
  //   Clock: Hz: 2147483647
  //   Registers
  //   ALU
  //   contents of Diode_Matrix (hex, n*v repeats v):
  //   0,10,20,c,4c,80,40,83,43,f
  //   Pipeline / Control
endmodule
