// Digital circuit adder.dig as structural Verilog
module adder (
  input  ClockIn,
  input  CarryFlag,
  input  [7:0] LHS,
  input  [7:0] RHS,
  input  CarrySelectA,
  input  CarrySelectB,
  output CarryOut,
  output [7:0] AdderOut
);

  wire _74283_1_pin9, CarrySelected, LHS__LatchOut0, LHS__LatchOut1, LHS__LatchOut2, LHS__LatchOut3,
       LHS__LatchOut4, LHS__LatchOut5, LHS__LatchOut6, LHS__LatchOut7, RHS__LatchOut0, RHS__LatchOut1,
       RHS__LatchOut2, RHS__LatchOut3, RHS__LatchOut4, RHS__LatchOut5, RHS__LatchOut6, RHS__LatchOut7;

  _74574 _74574_1 (
    .pin1(1'b0), .pin2(LHS[0]), .pin3(LHS[1]), .pin4(LHS[2]), .pin5(LHS[3]), .pin6(LHS[4]), .pin7(LHS[5]),
    .pin8(LHS[6]), .pin9(LHS[7]), .pin10(1'b0), .pin11(ClockIn), .pin12(LHS__LatchOut7),
    .pin13(LHS__LatchOut6), .pin14(LHS__LatchOut5), .pin15(LHS__LatchOut4), .pin16(LHS__LatchOut3),
    .pin17(LHS__LatchOut2), .pin18(LHS__LatchOut1), .pin19(LHS__LatchOut0), .pin20(1'b1));
  _74574 _74574_2 (
    .pin1(1'b0), .pin2(RHS[0]), .pin3(RHS[1]), .pin4(RHS[2]), .pin5(RHS[3]), .pin6(RHS[4]), .pin7(RHS[5]),
    .pin8(RHS[6]), .pin9(RHS[7]), .pin10(1'b0), .pin11(ClockIn), .pin12(RHS__LatchOut7),
    .pin13(RHS__LatchOut6), .pin14(RHS__LatchOut5), .pin15(RHS__LatchOut4), .pin16(RHS__LatchOut3),
    .pin17(RHS__LatchOut2), .pin18(RHS__LatchOut1), .pin19(RHS__LatchOut0), .pin20(1'b1));
  _74253 _74253_1 (
    .pin1(1'b0), .pin2(CarrySelectB), .pin3(1'b0), .pin4(1'b1), .pin5(CarryFlag), .pin6(1'b0),
    .pin7(CarrySelected), .pin8(1'b0), .pin9(1'b0), .pin10(1'b0), .pin11(1'b0), .pin12(1'b0), .pin13(1'b0),
    .pin14(CarrySelectA), .pin15(1'b0), .pin16(1'b1));
  _74283 _74283_1 (
    .pin1(AdderOut[1]), .pin2(RHS__LatchOut1), .pin3(LHS__LatchOut1), .pin4(AdderOut[0]),
    .pin5(LHS__LatchOut0), .pin6(RHS__LatchOut0), .pin7(CarrySelected), .pin8(1'b0), .pin9(_74283_1_pin9),
    .pin10(AdderOut[3]), .pin11(RHS__LatchOut3), .pin12(LHS__LatchOut3), .pin13(AdderOut[2]),
    .pin14(LHS__LatchOut2), .pin15(RHS__LatchOut2), .pin16(1'b1));
  _74283 _74283_2 (
    .pin1(AdderOut[5]), .pin2(RHS__LatchOut5), .pin3(LHS__LatchOut5), .pin4(AdderOut[4]),
    .pin5(LHS__LatchOut4), .pin6(RHS__LatchOut4), .pin7(_74283_1_pin9), .pin8(1'b0), .pin9(CarryOut),
    .pin10(AdderOut[7]), .pin11(RHS__LatchOut7), .pin12(LHS__LatchOut7), .pin13(AdderOut[6]),
    .pin14(LHS__LatchOut6), .pin15(RHS__LatchOut6), .pin16(1'b1));

  // Notes on the sheet:
  //   Carry Selection
endmodule

/* Test case Basic Tests:
ClockIn LHS RHS CarryFlag CarrySelectB CarrySelectA CarryOut AdderOut

# clear to predictable state
0       0   0   0         0            1            x        x
1       0   0   0         0            1            0        0

# add two numbers
0       12  8   0         0            1            x        x
1       12  8   0         0            1            0        20
  # verify that output persists through falling edge
0       0   0   0         0            1            0        20

# add two numbers with carry
0       8   8   0         0            1            x        x
1       8   8   1         0            1            0        17
  # verify that output persists through falling edge
  # carry flag is latched in the flags, so it's unexpected for it to change on the falling edge
  # if it did, the result would change
0       0   0   1         0            1            0        17

# add two numbers that overflow
0       255 1   0         0            1            x        x
1       255 1   0         0            1            1        0

# add 255 + carry = overflow
0       255 0   1         0            1            x        x
1       255 0   1         0            1            1        0

# add two numbers that overflow and nonzero result
0       128 255 0         0            1            x        x
1       128 255 0         0            1            1        127
*/
