// Digital circuit alu.dig as structural Verilog
module alu (
  input  CarrySelectB,
  input  CarrySelectA,
  input  [7:0] LHSIn,
  input  [7:0] RHSIn,
  input  ClockIn,
  input  ShiftSelectB,
  input  ShiftSelectA,
  output ArithCarryFlag,
  output [7:0] AdderOut,
  output LogicCarryFlag,
  output ZeroFlag,
  output SignFlag,
  output OverflowFlag
);

  wire ArithCarry, LogicCarry;
  wire [7:0] LHSOut;

  shift shift_1 (
    .SelectA(ShiftSelectA), .SelectB(ShiftSelectB), .LHSIn(LHSIn), .CarryIn(LogicCarryFlag),
    .CarryOut(LogicCarry), .LHSOut(LHSOut));
  adder adder_1 (
    .ClockIn(ClockIn), .CarryFlag(ArithCarryFlag), .LHS(LHSOut), .RHS(RHSIn), .CarrySelectA(CarrySelectA),
    .CarrySelectB(CarrySelectB), .CarryOut(ArithCarry), .AdderOut(AdderOut));
  flags flags_1 (
    .ClockIn(ClockIn), .ArithCarryIn(ArithCarry), .DataIn(AdderOut), .LogicCarryIn(LogicCarry), .LHS(LHSIn),
    .RHS(RHSIn), .ArithCarryFlag(ArithCarryFlag), .ZeroFlag(ZeroFlag), .LogicCarryFlag(LogicCarryFlag),
    .SignFlag(SignFlag), .OverflowFlag(OverflowFlag));

  // Other names for the same wires on the sheet: Data[7:0] = AdderOut; LHS[7:0] = LHSIn; RHS[7:0] = RHSIn
endmodule
