// Digital circuit flags.dig as structural Verilog
module flags (
  input  ClockIn,
  input  ArithCarryIn,
  input  [7:0] DataIn,
  input  LogicCarryIn,
  input  [7:0] LHS,
  input  [7:0] RHS,
  input  CarrySelectA,
  input  CarrySelectB,
  output ArithCarryFlag,
  output ZeroFlag,
  output LogicCarryFlag,
  output SignFlag,
  output OverflowFlag,
  output CarrySelectADelayed,
  output CarrySelectBDelayed
);

  wire _74260_1_pin5, _74260_1_pin6, Overflow, xor_1_out, xor_2_out;

  and and_1 (ZeroFlag, _74260_1_pin6, _74260_1_pin5);
  _74260 _74260_1 (
    .pin1(DataIn[0]), .pin2(DataIn[1]), .pin3(DataIn[2]), .pin4(DataIn[4]), .pin5(_74260_1_pin5),
    .pin6(_74260_1_pin6), .pin7(1'b0), .pin8(1'b0), .pin9(DataIn[7]), .pin10(DataIn[6]), .pin11(DataIn[5]),
    .pin12(DataIn[3]), .pin13(1'b0), .pin14(1'b1));
  xor xor_1 (xor_1_out, LHS[7], DataIn[7]);
  xor xor_2 (xor_2_out, DataIn[7], RHS[7]);
  and and_2 (Overflow, xor_1_out, xor_2_out);
  _74574 _74574_1 (
    .pin1(1'b0), .pin2(1'b0), .pin3(1'b0), .pin4(CarrySelectA), .pin5(CarrySelectB), .pin6(Overflow),
    .pin7(DataIn[7]), .pin8(LogicCarryIn), .pin9(ArithCarryIn), .pin10(1'b0), .pin11(ClockIn),
    .pin12(ArithCarryFlag), .pin13(LogicCarryFlag), .pin14(SignFlag), .pin15(OverflowFlag),
    .pin16(CarrySelectBDelayed), .pin17(CarrySelectADelayed), .pin20(1'b1));  // open: pin18, pin19
endmodule

/* Test case Zero Flag Tests:
ClockIn DataIn ZeroFlag
0       12     x
C       12     0
C       0      1
C       1      0
*/

/* Test case Arith Carry Flag Tests:
ClockIn ArithCarryIn ArithCarryFlag
0       0            x
C       1            1
C       0            0
*/

/* Test case Logic Carry Flag Tests:
ClockIn LogicCarryIn LogicCarryFlag
0       0            x
C       1            1
C       0            0
*/

/* Test case Sign Flag Tests:
ClockIn DataIn     SignFlag
0       0          x
C       0b00000000 0
C       0b10000000 1
*/

/* Test case Overflow Flag Tests:
ClockIn DataIn     RHS        LHS        OverflowFlag
0       0          0          0          x

# individual tests of all cases
C       0b00000000 0b00000000 0b00000000 x
C       0b00000000 0b00000000 0b00000000 0

C       0b00000000 0b00000000 0b10000000 x
C       0b00000000 0b00000000 0b10000000 0

C       0b00000000 0b10000000 0b00000000 x
C       0b00000000 0b10000000 0b00000000 0

C       0b00000000 0b10000000 0b10000000 x
C       0b00000000 0b10000000 0b10000000 1

C       0b10000000 0b00000000 0b00000000 x
C       0b10000000 0b00000000 0b00000000 1

C       0b10000000 0b00000000 0b10000000 x
C       0b10000000 0b00000000 0b10000000 0

C       0b10000000 0b10000000 0b00000000 x
C       0b10000000 0b10000000 0b00000000 0

C       0b10000000 0b10000000 0b10000000 x
C       0b10000000 0b10000000 0b10000000 0

# clear
0       0          0          0          x

# back-to-back tests (results are delayed by on clock)
# TODO they don't seem to be delayed, is this a bug?
C       0b00000000 0b00000000 0b00000000 0
C       0b00000000 0b00000000 0b10000000 0
C       0b00000000 0b10000000 0b00000000 0
C       0b00000000 0b10000000 0b10000000 1
C       0b10000000 0b00000000 0b00000000 1
C       0b10000000 0b00000000 0b10000000 0
C       0b10000000 0b10000000 0b00000000 0
C       0b10000000 0b10000000 0b10000000 0
C       0b00000000 0b00000000 0b00000000 0
*/
