// Digital circuit logic.dig as structural Verilog
module \logic  (
  input  Clock,
  input  [3:0] LogicSelect,
  input  [7:0] RHS,
  input  [7:0] LHS,
  output [7:0] RHSOut
);

  wire [7:0] universal_logic_8bit_1_y;

  universal_logic_8bit universal_logic_8bit_1 (
    .nOE(1'b0), .LogicSelect(LogicSelect), .B(RHS), .A(LHS), .Y(universal_logic_8bit_1_y));
  _74574 _74574_1 (
    .pin1(1'b0), .pin2(universal_logic_8bit_1_y[7]), .pin3(universal_logic_8bit_1_y[6]),
    .pin4(universal_logic_8bit_1_y[5]), .pin5(universal_logic_8bit_1_y[4]),
    .pin6(universal_logic_8bit_1_y[3]), .pin7(universal_logic_8bit_1_y[2]),
    .pin8(universal_logic_8bit_1_y[1]), .pin9(universal_logic_8bit_1_y[0]), .pin10(1'b0), .pin11(Clock),
    .pin12(RHSOut[0]), .pin13(RHSOut[1]), .pin14(RHSOut[2]), .pin15(RHSOut[3]), .pin16(RHSOut[4]),
    .pin17(RHSOut[5]), .pin18(RHSOut[6]), .pin19(RHSOut[7]), .pin20(1'b1));
endmodule
