// Digital circuit universal-logic-8bit.dig as structural Verilog
module universal_logic_8bit (
  input  nOE,
  input  [3:0] LogicSelect,
  input  [7:0] B,
  input  [7:0] A,
  output [7:0] Y
);

  _74253 _74253_1 (
    .pin1(1'b0), .pin2(B[0]), .pin3(1'b0), .pin4(1'b0), .pin5(1'b0), .pin6(1'b0), .pin8(1'b0), .pin9(Y[0]),
    .pin10(LogicSelect[0]), .pin11(LogicSelect[1]), .pin12(LogicSelect[2]), .pin13(LogicSelect[3]),
    .pin14(A[0]), .pin15(nOE), .pin16(1'b1));  // open: pin7
  _74253 _74253_2 (
    .pin1(1'b0), .pin2(B[4]), .pin3(1'b0), .pin4(1'b0), .pin5(1'b0), .pin6(1'b0), .pin8(1'b0), .pin9(Y[4]),
    .pin10(LogicSelect[0]), .pin11(LogicSelect[1]), .pin12(LogicSelect[2]), .pin13(LogicSelect[3]),
    .pin14(A[4]), .pin15(nOE), .pin16(1'b1));  // open: pin7
  _74253 _74253_3 (
    .pin1(1'b0), .pin2(B[1]), .pin3(1'b0), .pin4(1'b0), .pin5(1'b0), .pin6(1'b0), .pin8(1'b0), .pin9(Y[1]),
    .pin10(LogicSelect[0]), .pin11(LogicSelect[1]), .pin12(LogicSelect[2]), .pin13(LogicSelect[3]),
    .pin14(A[1]), .pin15(nOE), .pin16(1'b1));  // open: pin7
  _74253 _74253_4 (
    .pin1(1'b0), .pin2(B[5]), .pin3(1'b0), .pin4(1'b0), .pin5(1'b0), .pin6(1'b0), .pin8(1'b0), .pin9(Y[5]),
    .pin10(LogicSelect[0]), .pin11(LogicSelect[1]), .pin12(LogicSelect[2]), .pin13(LogicSelect[3]),
    .pin14(A[5]), .pin15(nOE), .pin16(1'b1));  // open: pin7
  _74253 _74253_5 (
    .pin1(1'b0), .pin2(B[2]), .pin3(1'b0), .pin4(1'b0), .pin5(1'b0), .pin6(1'b0), .pin8(1'b0), .pin9(Y[2]),
    .pin10(LogicSelect[0]), .pin11(LogicSelect[1]), .pin12(LogicSelect[2]), .pin13(LogicSelect[3]),
    .pin14(A[2]), .pin15(nOE), .pin16(1'b1));  // open: pin7
  _74253 _74253_6 (
    .pin1(1'b0), .pin2(B[6]), .pin3(1'b0), .pin4(1'b0), .pin5(1'b0), .pin6(1'b0), .pin8(1'b0), .pin9(Y[6]),
    .pin10(LogicSelect[0]), .pin11(LogicSelect[1]), .pin12(LogicSelect[2]), .pin13(LogicSelect[3]),
    .pin14(A[6]), .pin15(nOE), .pin16(1'b1));  // open: pin7
  _74253 _74253_7 (
    .pin1(1'b0), .pin2(B[3]), .pin3(1'b0), .pin4(1'b0), .pin5(1'b0), .pin6(1'b0), .pin8(1'b0), .pin9(Y[3]),
    .pin10(LogicSelect[0]), .pin11(LogicSelect[1]), .pin12(LogicSelect[2]), .pin13(LogicSelect[3]),
    .pin14(A[3]), .pin15(nOE), .pin16(1'b1));  // open: pin7
  _74253 _74253_8 (
    .pin1(1'b0), .pin2(B[7]), .pin3(1'b0), .pin4(1'b0), .pin5(1'b0), .pin6(1'b0), .pin8(1'b0), .pin9(Y[7]),
    .pin10(LogicSelect[0]), .pin11(LogicSelect[1]), .pin12(LogicSelect[2]), .pin13(LogicSelect[3]),
    .pin14(A[7]), .pin15(nOE), .pin16(1'b1));  // open: pin7
endmodule

/* Test case Basic Tests:
~OE	LogicSelect	B		A		Y
# output enable test
1	0x0		0		0		z

# always LOW
0	0x0		0b11001100	0b10101010	0b00000000
# nor
0	0x1		0b11001100	0b10101010	0b00010001
# A !B
0	0x2		0b11001100	0b10101010	0b00100010
# !B Pass
0	0x3		0b11001100	0b10101010	0b00110011
# !A B
0	0x4		0b11001100	0b10101010	0b01000100
# !A Pass
0	0x5		0b11001100	0b10101010	0b01010101
# XOR
0	0x6		0b11001100	0b10101010	0b01100110
# NAND
0	0x7		0b11001100	0b10101010	0b01110111
# AND
0	0x8		0b11001100	0b10101010	0b10001000
# XNOR
0	0x9		0b11001100	0b10101010	0b10011001
# A Pass
0	0xa		0b11001100	0b10101010	0b10101010
# !B+A
0	0xb		0b11001100	0b10101010	0b10111011
# B Pass
0	0xc		0b11001100	0b10101010	0b11001100
# B+!A
0	0xd		0b11001100	0b10101010	0b11011101
# OR
0	0xe		0b11001100	0b10101010	0b11101110
# always HIGH
0	0xf		0b11001100	0b10101010	0b11111111
*/
