// Digital circuit buscontrol.dig as structural Verilog
module buscontrol (
  input  ClockIn,
  input  LHS__0,
  input  LHS__1,
  input  RHS__0,
  input  RHS__1,
  input  ResetIn,
  input  MainBus__Assert__0,
  input  MainBus__Assert__1,
  input  MainBus__Assert__2,
  input  MainBus__Assert__3,
  input  MainBus__Load__0,
  input  MainBus__Load__1,
  input  MainBus__Load__2,
  input  MainBus__Load__3,
  input  Inc__PCRA__0,
  input  Inc__PCRA__1,
  input  Inc__SPSIDI__0,
  input  Inc__SPSIDI__1,
  input  Xfer__Assert0,
  input  Xfer__Assert1,
  input  Xfer__Assert2,
  input  Xfer__LoadDec0,
  input  Xfer__LoadDec1,
  input  Xfer__LoadDec2,
  input  Xfer__LoadDec3,
  input  AddrSel0,
  input  AddrSel1,
  input  AddrSel2,
  output Reg__A__LHS,
  output Reg__B__LHS,
  output Reg__C__LHS,
  output Reg__D__LHS,
  output Reg__A__RHS,
  output Reg__B__RHS,
  output Reg__C__RHS,
  output Reg__D__RHS,
  output Reg__A__Assert,
  output Reg__B__Assert,
  output Reg__C__Assert,
  output Reg__D__Assert,
  output Reg__Const__Assert,
  output Reg__TL__Assert,
  output Reg__TH__Assert,
  output Alu__Assert,
  output Dev9__Assert,
  output Dev10__Assert,
  output Dev11__Assert,
  output Dev12__Assert,
  output Dev13__Assert,
  output Dev14__Assert,
  output MemBridge__Assert,
  output Reg__A__Load,
  output Reg__B__Load,
  output Reg__C__Load,
  output Reg__D__Load,
  output Reg__Const__Load,
  output Reg__TL__Load,
  output Reg__TH__Load,
  output Alu__Load,
  output Dev9__Load,
  output Dev10__Load,
  output Dev11__Load,
  output Dev12__Load,
  output Dev13__Load,
  output Dev14__Load,
  output MemBridge__Load,
  output MemBridge__Direction,
  output Reg__PCRA0__Inc,
  output Reg__PCRA1__Inc,
  output Reg__SP__Inc,
  output Reg__SI__Inc,
  output Reg__DI__Inc,
  output Reg__PCRA0__AXfer,
  output Reg__PCRA1__AXfer,
  output Reg__SP__AXfer,
  output Reg__SI__AXfer,
  output Reg__DI__AXfer,
  output Reg__TX__AXfer,
  output Reg__TX__AMode,
  output Reg__PCRA0__LXfer,
  output Reg__PCRA1__LXfer,
  output Reg__SP__LXfer,
  output Reg__SI__LXfer,
  output Reg__DI__LXfer,
  output Reg__TX__LXfer,
  output Reg__Const__LMem,
  output Reg__PCRA0__Dec,
  output Reg__PCRA1__Dec,
  output Reg__SP__Dec,
  output Reg__SI__Dec,
  output Reg__DI__Dec,
  output Memory__Ack,
  output Reg__PCRA0__AAddr,
  output Reg__PCRA1__AAddr,
  output Reg__SP__AAddr,
  output Reg__SI__AAddr,
  output Reg__DI__AAddr,
  output Reg__TX__AAddr
);

  wire AddressRegisterClear, AddressRegisterClock, DelayedClock, DelayedClockInverted, not_1_out, not_2_out,
       not_3_out, not_4_out, not_8_out;

  not not_1 (not_1_out, ClockIn);
  not not_2 (not_2_out, not_1_out);
  not not_3 (not_3_out, not_2_out);
  not not_4 (not_4_out, not_3_out);
  not not_5 (DelayedClockInverted, DelayedClock);
  not not_6 (AddressRegisterClock, DelayedClockInverted);
  not not_7 (AddressRegisterClear, ResetIn);
  not not_8 (not_8_out, not_4_out);
  not not_9 (DelayedClock, not_8_out);
  _74138 LHS_Assert (
    .pin1(LHS__0), .pin2(LHS__1), .pin3(1'b0), .pin4(1'b0), .pin5(1'b0), .pin6(1'b1), .pin8(1'b0),
    .pin12(Reg__D__LHS), .pin13(Reg__C__LHS), .pin14(Reg__B__LHS), .pin15(Reg__A__LHS), .pin16(1'b1));  // open: pin7, pin9, pin10, pin11
  _74138 MainBus_Assert_3_eq_L (
    .pin1(MainBus__Assert__0), .pin2(MainBus__Assert__1), .pin3(MainBus__Assert__2),
    .pin4(MainBus__Assert__3), .pin5(1'b0), .pin6(1'b1), .pin7(Reg__TH__Assert), .pin8(1'b0),
    .pin9(Reg__TL__Assert), .pin10(Reg__Const__Assert), .pin11(Reg__D__Assert), .pin12(Reg__C__Assert),
    .pin13(Reg__B__Assert), .pin14(Reg__A__Assert), .pin16(1'b1));  // open: pin15
  _74138 MainBus_Assert_3_eq_H (
    .pin1(MainBus__Assert__0), .pin2(MainBus__Assert__1), .pin3(MainBus__Assert__2), .pin4(1'b0),
    .pin5(1'b0), .pin6(MainBus__Assert__3), .pin7(MemBridge__Assert), .pin8(1'b0), .pin9(Dev14__Assert),
    .pin10(Dev13__Assert), .pin11(Dev12__Assert), .pin12(Dev11__Assert), .pin13(Dev10__Assert),
    .pin14(Dev9__Assert), .pin15(Alu__Assert), .pin16(1'b1));
  _74138 Program_Counter_INC (
    .pin1(Inc__PCRA__0), .pin2(Inc__PCRA__1), .pin3(1'b0), .pin4(1'b0), .pin5(DelayedClockInverted),
    .pin6(1'b1), .pin8(1'b0), .pin14(Reg__PCRA1__Inc), .pin15(Reg__PCRA0__Inc), .pin16(1'b1));  // open: pin7, pin9, pin10, pin11, pin12, pin13
  _74138 Transfer_Assert (
    .pin1(Xfer__Assert0), .pin2(Xfer__Assert1), .pin3(Xfer__Assert2), .pin4(1'b0), .pin5(1'b0), .pin6(1'b1),
    .pin7(Reg__TX__AMode), .pin8(1'b0), .pin9(Reg__TX__AXfer), .pin10(Reg__DI__AXfer),
    .pin11(Reg__SI__AXfer), .pin12(Reg__SP__AXfer), .pin13(Reg__PCRA1__AXfer), .pin14(Reg__PCRA0__AXfer),
    .pin16(1'b1));  // open: pin15
  _74138 Address_Bus_Assert (
    .pin1(AddrSel0), .pin2(AddrSel1), .pin3(AddrSel2), .pin4(1'b0), .pin5(1'b0), .pin6(1'b1), .pin8(1'b0),
    .pin9(Reg__TX__AAddr), .pin10(Reg__DI__AAddr), .pin11(Reg__SI__AAddr), .pin12(Reg__SP__AAddr),
    .pin13(Reg__PCRA1__AAddr), .pin14(Reg__PCRA0__AAddr), .pin15(Memory__Ack), .pin16(1'b1));  // open: pin7
  _74138 RHS_Assert (
    .pin1(RHS__0), .pin2(RHS__1), .pin3(1'b0), .pin4(1'b0), .pin5(1'b0), .pin6(1'b1), .pin8(1'b0),
    .pin12(Reg__D__RHS), .pin13(Reg__C__RHS), .pin14(Reg__B__RHS), .pin15(Reg__A__RHS), .pin16(1'b1));  // open: pin7, pin9, pin10, pin11
  _74138 MainBus_Load_3_eq_L (
    .pin1(MainBus__Load__0), .pin2(MainBus__Load__1), .pin3(MainBus__Load__2), .pin4(MainBus__Load__3),
    .pin5(DelayedClockInverted), .pin6(1'b1), .pin7(Reg__TH__Load), .pin8(1'b0), .pin9(Reg__TL__Load),
    .pin10(Reg__Const__Load), .pin11(Reg__D__Load), .pin12(Reg__C__Load), .pin13(Reg__B__Load),
    .pin14(Reg__A__Load), .pin16(1'b1));  // open: pin15
  _74138 MainBus_Load_3_eq_H (
    .pin1(MainBus__Load__0), .pin2(MainBus__Load__1), .pin3(MainBus__Load__2), .pin4(1'b0),
    .pin5(DelayedClockInverted), .pin6(MainBus__Load__3), .pin7(MemBridge__Load), .pin8(1'b0),
    .pin9(Dev14__Load), .pin10(Dev13__Load), .pin11(Dev12__Load), .pin12(Dev11__Load), .pin13(Dev10__Load),
    .pin14(Dev9__Load), .pin15(Alu__Load), .pin16(1'b1));
  _74138 SP__SI__DI_INC (
    .pin1(Inc__SPSIDI__0), .pin2(Inc__SPSIDI__1), .pin3(1'b0), .pin4(1'b0), .pin5(DelayedClockInverted),
    .pin6(1'b1), .pin8(1'b0), .pin12(Reg__DI__Inc), .pin13(Reg__SI__Inc), .pin14(Reg__SP__Inc), .pin16(1'b1));  // open: pin7, pin9, pin10, pin11, pin15
  _74138 Transfer_Load_Dec_3_eq_L (
    .pin1(Xfer__LoadDec0), .pin2(Xfer__LoadDec1), .pin3(Xfer__LoadDec2), .pin4(Xfer__LoadDec3),
    .pin5(DelayedClockInverted), .pin6(1'b1), .pin8(1'b0), .pin9(Reg__TX__LXfer), .pin10(Reg__DI__LXfer),
    .pin11(Reg__SI__LXfer), .pin12(Reg__SP__LXfer), .pin13(Reg__PCRA1__LXfer), .pin14(Reg__PCRA0__LXfer),
    .pin16(1'b1));  // open: pin7, pin15
  _74138 MemBridge_Direction (
    .pin1(MainBus__Load__0), .pin2(MainBus__Load__1), .pin3(MainBus__Load__2), .pin4(1'b0), .pin5(1'b0),
    .pin6(MainBus__Load__3), .pin7(MemBridge__Direction), .pin8(1'b0), .pin16(1'b1));  // open: pin9, pin10, pin11, pin12, pin13, pin14, pin15
  _74138 Transfer_Load_Dec_3_eq_H (
    .pin1(Xfer__LoadDec0), .pin2(Xfer__LoadDec1), .pin3(Xfer__LoadDec2), .pin4(1'b0),
    .pin5(DelayedClockInverted), .pin6(Xfer__LoadDec3), .pin8(1'b0), .pin10(Reg__DI__Dec),
    .pin11(Reg__SI__Dec), .pin12(Reg__SP__Dec), .pin13(Reg__PCRA1__Dec), .pin14(Reg__PCRA0__Dec),
    .pin15(Reg__Const__LMem), .pin16(1'b1));  // open: pin7, pin9

  // Notes on the sheet:
  //   Delaying clock like this probably won't work for the FPGA.
endmodule
