// Digital circuit clock_reset.dig as structural Verilog
module clock_reset (
  input  ClockIn,
  input  ResetIn,
  output ResetOut,
  output nResetOut
);

  wire C0, C1, C2, C3, CountDown, LatchReset;

  LED led_1 (.in(C3));
  LED led_2 (.in(C2));
  LED led_3 (.in(C1));
  LED led_4 (.in(C0));
  LED led_5 (.in(ResetOut));
  LED led_6 (.in(nResetOut));
  _74193 _74193_1 (
    .pin1(1'b0), .pin2(C1), .pin3(C0), .pin4(CountDown), .pin5(1'b1), .pin6(C2), .pin7(C3), .pin8(1'b0),
    .pin9(1'b0), .pin10(1'b1), .pin11(ResetIn), .pin13(LatchReset), .pin14(1'b0), .pin15(1'b0), .pin16(1'b1));  // open: pin12
  _7400 _7400_1 (
    .pin1(ResetOut), .pin2(ResetIn), .pin3(nResetOut), .pin4(nResetOut), .pin5(LatchReset), .pin6(ResetOut),
    .pin7(1'b0), .pin8(CountDown), .pin9(nResetOut), .pin10(ClockIn), .pin12(1'b1), .pin13(1'b1), .pin14(1'b1));  // open: pin11

  // Other names for the same wires on the sheet: Clock = ClockIn; LatchQ = ResetOut; nLatchQ = nResetOut;
  //   Reset = ResetIn

  // Notes on the sheet:
  //   ResetIn: default 1
endmodule
