// Digital circuit mainbus.dig as structural Verilog
module mainbus (
  input  ClockIn,
  input  LHS__0,
  input  LHS__1,
  input  RHS__0,
  input  RHS__1,
  input  MainBus__Assert__0,
  input  MainBus__Assert__1,
  input  MainBus__Assert__2,
  input  MainBus__Assert__3,
  input  MainBus__Load__0,
  input  MainBus__Load__1,
  input  MainBus__Load__2,
  input  MainBus__Load__3,
  input  [7:0] MainBus,
  input  Inc__PCRA__0,
  input  Inc__PCRA__1,
  input  Inc__SPSIDI__0,
  input  Inc__SPSIDI__1,
  input  Xfer__Assert0,
  input  Xfer__Assert1,
  input  Xfer__Assert2,
  input  Xfer__LoadDec0,
  input  Xfer__LoadDec1,
  input  Xfer__LoadDec2,
  input  Xfer__LoadDec3,
  input  AddrSel0,
  input  AddrSel1,
  input  AddrSel2,
  input  Reset,
  input  [7:0] LHSBus,
  input  [7:0] RHSBus
);

  wire dipswitch_1_out, dipswitch_2_out, dipswitch_3_out, Reg__A__Assert, Reg__A__LHS, Reg__A__Load,
       Reg__A__RHS, Reg__B__Assert, Reg__B__LHS, Reg__B__Load, Reg__B__RHS, Reg__C__Assert, Reg__C__LHS,
       Reg__C__Load, Reg__C__RHS, Reg__Const__Assert, Reg__Const__Load, Reg__D__Assert, Reg__D__LHS,
       Reg__D__Load, Reg__D__RHS, Reg__TH__Assert, Reg__TH__Load, Reg__TL__Assert, Reg__TL__Load;
  wire [7:0] LHSBus_t, MainBus_t, RHSBus_t;

  buscontrol buscontrol_1 (
    .ClockIn(ClockIn), .ResetIn(LHS__0), .MainBus__Assert__0(LHS__1), .MainBus__Assert__1(RHS__0),
    .MainBus__Assert__2(RHS__1), .MainBus__Assert__3(Reset), .MainBus__Load__0(MainBus__Assert__0),
    .MainBus__Load__1(MainBus__Assert__1), .MainBus__Load__2(MainBus__Assert__2),
    .MainBus__Load__3(MainBus__Assert__3), .Inc__SPSIDI__0(MainBus__Load__0),
    .Inc__SPSIDI__1(MainBus__Load__1), .AddrSel0(MainBus__Load__2), .AddrSel1(MainBus__Load__3),
    .AddrSel2(Inc__PCRA__0), .LHS__0(Inc__PCRA__1), .LHS__1(Inc__SPSIDI__0), .RHS__0(Inc__SPSIDI__1),
    .RHS__1(Xfer__Assert0), .Xfer__Assert0(Xfer__Assert1), .Xfer__Assert1(Xfer__Assert2),
    .Xfer__Assert2(Xfer__LoadDec0), .Xfer__LoadDec0(Xfer__LoadDec1), .Xfer__LoadDec1(Xfer__LoadDec2),
    .Xfer__LoadDec2(Xfer__LoadDec3), .Xfer__LoadDec3(AddrSel0), .Inc__PCRA__0(AddrSel1),
    .Inc__PCRA__1(AddrSel2), .Reg__A__LHS(Reg__A__LHS), .Reg__B__LHS(Reg__B__LHS), .Reg__C__LHS(Reg__C__LHS),
    .Reg__D__LHS(Reg__D__LHS), .Reg__A__RHS(Reg__A__RHS), .Reg__B__RHS(Reg__B__RHS),
    .Reg__C__RHS(Reg__C__RHS), .Reg__D__RHS(Reg__D__RHS), .Reg__A__Assert(Reg__A__Assert),
    .Reg__B__Assert(Reg__B__Assert), .Reg__C__Assert(Reg__C__Assert), .Reg__D__Assert(Reg__D__Assert),
    .Reg__Const__Assert(Reg__Const__Assert), .Reg__TL__Assert(Reg__TL__Assert),
    .Reg__TH__Assert(Reg__TH__Assert), .Reg__A__Load(Reg__A__Load), .Reg__B__Load(Reg__B__Load),
    .Reg__C__Load(Reg__C__Load), .Reg__D__Load(Reg__D__Load), .Reg__Const__Load(Reg__Const__Load),
    .Reg__TL__Load(Reg__TL__Load), .Reg__TH__Load(Reg__TH__Load));  // open: Alu__Assert, Dev9__Assert, Dev10__Assert, Dev11__Assert, Dev12__Assert, Dev13__Assert, Dev14__Assert, MemBridge__Assert, Alu__Load, Dev9__Load, Dev10__Load, Dev11__Load, Dev12__Load, Dev13__Load, Dev14__Load, MemBridge__Load, MemBridge__Direction, Reg__PCRA0__Inc, Reg__PCRA1__Inc, Reg__SP__Inc, Reg__SI__Inc, Reg__DI__Inc, Reg__PCRA0__AXfer, Reg__PCRA1__AXfer, Reg__SP__AXfer, Reg__SI__AXfer, Reg__DI__AXfer, Reg__TX__AXfer, Reg__TX__AMode, Reg__PCRA0__LXfer, Reg__PCRA1__LXfer, Reg__SP__LXfer, Reg__SI__LXfer, Reg__DI__LXfer, Reg__TX__LXfer, Reg__Const__LMem, Reg__PCRA0__Dec, Reg__PCRA1__Dec, Reg__SP__Dec, Reg__SI__Dec, Reg__DI__Dec, Memory__Ack, Reg__PCRA0__AAddr, Reg__PCRA1__AAddr, Reg__SP__AAddr, Reg__SI__AAddr, Reg__DI__AAddr, Reg__TX__AAddr
  reg_8bit_generalpurpose A (
    .MainBusIn(MainBus_t), .Reg__Assert__RHS(Reg__A__RHS), .Reg__Assert__LHS(Reg__A__LHS),
    .Reg__Assert(Reg__A__Assert), .Reg__Load(Reg__A__Load), .MainBusOut(MainBus_t), .LHSBus(LHSBus_t),
    .RHSBus(RHSBus_t));
  reg_8bit_generalpurpose B (
    .MainBusIn(MainBus_t), .Reg__Assert__RHS(Reg__B__RHS), .Reg__Assert__LHS(Reg__B__LHS),
    .Reg__Assert(Reg__B__Assert), .Reg__Load(Reg__B__Load), .MainBusOut(MainBus_t), .LHSBus(LHSBus_t),
    .RHSBus(RHSBus_t));
  reg_8bit_generalpurpose C (
    .MainBusIn(MainBus_t), .Reg__Assert__RHS(Reg__C__RHS), .Reg__Assert__LHS(Reg__C__LHS),
    .Reg__Assert(Reg__C__Assert), .Reg__Load(Reg__C__Load), .MainBusOut(MainBus_t), .LHSBus(LHSBus_t),
    .RHSBus(RHSBus_t));
  reg_8bit_generalpurpose D (
    .MainBusIn(MainBus_t), .Reg__Assert__RHS(Reg__D__RHS), .Reg__Assert__LHS(Reg__D__LHS),
    .Reg__Assert(Reg__D__Assert), .Reg__Load(Reg__D__Load), .MainBusOut(MainBus_t), .LHSBus(LHSBus_t),
    .RHSBus(RHSBus_t));
  DipSwitch dipswitch_1 (.out(dipswitch_1_out));
  PullUp #(.Bits(8)) pullup_1 (.out(MainBus_t));
  assign MainBus_t = dipswitch_1_out ? MainBus : 8'bz;  // Driver driver_1
  DipSwitch dipswitch_2 (.out(dipswitch_2_out));
  assign LHSBus_t = dipswitch_2_out ? LHSBus : 8'bz;  // Driver driver_2
  PullUp #(.Bits(8)) pullup_2 (.out(LHSBus_t));
  DipSwitch dipswitch_3 (.out(dipswitch_3_out));
  PullUp #(.Bits(8)) pullup_3 (.out(RHSBus_t));
  assign RHSBus_t = dipswitch_3_out ? RHSBus : 8'bz;  // Driver driver_3

  // Other names for the same wires on the sheet: Clock = ClockIn

  // Notes on the sheet:
  //   MainBus: default 105
  //   LHSBus: default 105
  //   RHSBus: default 105
  //   These Tri-States are temporary, makes it easier to test
endmodule
