// Digital circuit memory.dig as structural Verilog
module memory (
  input  [15:0] Addr,
  input  [7:0] MainBus,
  input  [7:0] MEMDATA,
  input  MemBridge__Direction,
  input  MemBridge__Load,
  input  MemBridge__Assert
);

  wire _74541_1_pin11, _74541_1_pin12, _74541_1_pin13, _74541_1_pin14, _74541_1_pin15, _74541_1_pin16,
       _74541_1_pin17, _74541_1_pin18, _74541_2_pin11, _74541_2_pin12, _74541_2_pin13, _74541_2_pin14,
       _74541_2_pin15, _74541_2_pin16, _74541_2_pin17, _74541_2_pin18, MEMDATA0, MEMDATA1, MEMDATA2,
       MEMDATA3, MEMDATA4, MEMDATA5, MEMDATA6, MEMDATA7, not_1_out, not_2_out, not_4_out, nOutputEnable,
       nRamCE, nRamWE, nRomCE;

  BusSplitter #(.Bits(8)) bussplitter_1 (
    .D(MEMDATA), .OE(nOutputEnable), .D0(MEMDATA0), .D1(MEMDATA1), .D2(MEMDATA2), .D3(MEMDATA3),
    .D4(MEMDATA4), .D5(MEMDATA5), .D6(MEMDATA6), .D7(MEMDATA7));
  not not_1 (not_1_out, MemBridge__Load);
  not not_2 (not_2_out, not_1_out);
  _74541 _74541_1 (
    .pin1(MemBridge__Assert), .pin2(MEMDATA[7]), .pin3(MEMDATA[6]), .pin4(MEMDATA[5]), .pin5(MEMDATA[4]),
    .pin6(MEMDATA[3]), .pin7(MEMDATA[2]), .pin8(MEMDATA[1]), .pin9(MEMDATA[0]), .pin10(1'b0),
    .pin11(_74541_1_pin11), .pin12(_74541_1_pin12), .pin13(_74541_1_pin13), .pin14(_74541_1_pin14),
    .pin15(_74541_1_pin15), .pin16(_74541_1_pin16), .pin17(_74541_1_pin17), .pin18(_74541_1_pin18),
    .pin19(1'b0), .pin20(1'b1));
  not not_3 (nOutputEnable, MemBridge__Direction);
  not not_4 (not_4_out, not_2_out);
  not not_5 (nRamWE, not_4_out);
  BusSplitter #(.Bits(8)) bussplitter_2 (
    .D(MainBus), .OE(MemBridge__Assert), .D0(_74541_1_pin11), .D1(_74541_1_pin12), .D2(_74541_1_pin13),
    .D3(_74541_1_pin14), .D4(_74541_1_pin15), .D5(_74541_1_pin16), .D6(_74541_1_pin17), .D7(_74541_1_pin18));
  _74138 _74138_1 (
    .pin1(Addr[15]), .pin2(1'b0), .pin3(1'b0), .pin4(1'b0), .pin5(1'b0), .pin6(1'b1), .pin8(1'b0),
    .pin14(nRamCE), .pin15(nRomCE), .pin16(1'b1));  // open: pin7, pin9, pin10, pin11, pin12, pin13
  _74541 _74541_2 (
    .pin1(MemBridge__Direction), .pin2(MainBus[7]), .pin3(MainBus[6]), .pin4(MainBus[5]), .pin5(MainBus[4]),
    .pin6(MainBus[3]), .pin7(MainBus[2]), .pin8(MainBus[1]), .pin9(MainBus[0]), .pin10(1'b0),
    .pin11(_74541_2_pin11), .pin12(_74541_2_pin12), .pin13(_74541_2_pin13), .pin14(_74541_2_pin14),
    .pin15(_74541_2_pin15), .pin16(_74541_2_pin16), .pin17(_74541_2_pin17), .pin18(_74541_2_pin18),
    .pin19(1'b0), .pin20(1'b1));
  BusSplitter #(.Bits(8)) bussplitter_3 (
    .D(MEMDATA), .OE(MemBridge__Direction), .D0(_74541_2_pin11), .D1(_74541_2_pin12), .D2(_74541_2_pin13),
    .D3(_74541_2_pin14), .D4(_74541_2_pin15), .D5(_74541_2_pin16), .D6(_74541_2_pin17), .D7(_74541_2_pin18));
  program_memory program_memory_1 (
    .nCE(nRomCE), .nOE(nOutputEnable), .nWE(1'b1), .VCC(1'b1), .GND(1'b0), .I_O0(MEMDATA0), .I_O1(MEMDATA1),
    .I_O2(MEMDATA2), .I_O3(MEMDATA3), .I_O4(MEMDATA4), .I_O5(MEMDATA5), .I_O6(MEMDATA6), .I_O7(MEMDATA7),
    .A0(Addr[0]), .A1(Addr[1]), .A2(Addr[2]), .A3(Addr[3]), .A4(Addr[4]), .A5(Addr[5]), .A6(Addr[6]),
    .A7(Addr[7]), .A8(Addr[8]), .A9(Addr[9]), .A10(Addr[10]), .A11(Addr[11]), .A12(Addr[12]), .A13(Addr[13]),
    .A14(Addr[14]));
  _62256 _62256_1 (
    .nCE(nRamCE), .nOE(nOutputEnable), .nWE(nRamWE), .VCC(1'b1), .GND(1'b0), .I_O0(MEMDATA0),
    .I_O1(MEMDATA1), .I_O2(MEMDATA2), .I_O3(MEMDATA3), .I_O4(MEMDATA4), .I_O5(MEMDATA5), .I_O6(MEMDATA6),
    .I_O7(MEMDATA7), .A0(Addr[0]), .A1(Addr[1]), .A2(Addr[2]), .A3(Addr[3]), .A4(Addr[4]), .A5(Addr[5]),
    .A6(Addr[6]), .A7(Addr[7]), .A8(Addr[8]), .A9(Addr[9]), .A10(Addr[10]), .A11(Addr[11]), .A12(Addr[12]),
    .A13(Addr[13]), .A14(Addr[14]));

  // Notes on the sheet:
  //   Addr: default 32768
  //   MemBridge__Load: default 1
  //   MemBridge__Assert: default 1
endmodule

/* Test case Simple Tests:
MemBridge\_Assert	MemBridge\_Load MemBridge\_Direction 	Addr 	MainBus	MainBus_out
# read from ROM
0			1		1			0x0000	z	0xC

# write to RAM
1			0		0			0x8000	0xFF	x
1			1		0			0x8000	0xFF	x

# verify write
0			1		1			0x8000	z	0xFF

# assert MEMDATA to MainBus
0			1		1			0x8000	z	0xFF
*/
