// Digital circuit reg-16bit-updownload.dig as structural Verilog
module reg_16bit_updownload (
  input  Clock,
  input  Clear,
  input  nAssertAddr,
  input  nAssertBus,
  input  nLoad,
  input  Inc,
  input  Dec,
  input  [15:0] Addr,
  input  [15:0] Bus,
  output nCarry,
  output nBorrow
);

  wire _74193_1_pin4, _74193_1_pin5, _74193_2_pin4, _74193_2_pin5, _74193_3_pin4, _74193_3_pin5, Addr0,
       Addr1, Addr2, Addr3, Addr4, Addr5, Addr6, Addr7, Addr8, Addr9, Addr10, Addr11, Addr12, Addr13, Addr14,
       Addr15, Bus0, Bus1, Bus2, Bus3, Bus4, Bus5, Bus6, Bus7, Bus8, Bus9, Bus10, Bus11, Bus12, Bus13, Bus14,
       Bus15;
  wire [3:0] _74193_1_pin7, _74193_2_pin7, _74193_3_pin7, _74193_4_pin7;

  BusSplitter #(.Bits(16)) bussplitter_1 (
    .D(Addr), .OE(nAssertAddr), .D0(Addr0), .D1(Addr1), .D2(Addr2), .D3(Addr3), .D4(Addr4), .D5(Addr5),
    .D6(Addr6), .D7(Addr7), .D8(Addr8), .D9(Addr9), .D10(Addr10), .D11(Addr11), .D12(Addr12), .D13(Addr13),
    .D14(Addr14), .D15(Addr15));
  BusSplitter #(.Bits(16)) bussplitter_2 (
    .D(Bus), .OE(nAssertBus), .D0(Bus0), .D1(Bus1), .D2(Bus2), .D3(Bus3), .D4(Bus4), .D5(Bus5), .D6(Bus6),
    .D7(Bus7), .D8(Bus8), .D9(Bus9), .D10(Bus10), .D11(Bus11), .D12(Bus12), .D13(Bus13), .D14(Bus14),
    .D15(Bus15));
  _74193 _74193_1 (
    .pin1(Bus[13]), .pin2(_74193_1_pin7[1]), .pin3(_74193_1_pin7[0]), .pin4(_74193_1_pin4),
    .pin5(_74193_1_pin5), .pin6(_74193_1_pin7[2]), .pin7(_74193_1_pin7[3]), .pin8(1'b0), .pin9(Bus[15]),
    .pin10(Bus[14]), .pin11(nLoad), .pin12(nCarry), .pin13(nBorrow), .pin14(Clear), .pin15(Bus[12]),
    .pin16(1'b1));
  _74193 _74193_2 (
    .pin1(Bus[9]), .pin2(_74193_2_pin7[1]), .pin3(_74193_2_pin7[0]), .pin4(_74193_2_pin4),
    .pin5(_74193_2_pin5), .pin6(_74193_2_pin7[2]), .pin7(_74193_2_pin7[3]), .pin8(1'b0), .pin9(Bus[11]),
    .pin10(Bus[10]), .pin11(nLoad), .pin12(_74193_1_pin5), .pin13(_74193_1_pin4), .pin14(Clear),
    .pin15(Bus[8]), .pin16(1'b1));
  _74574 _74574_1 (
    .pin1(nAssertAddr), .pin2(_74193_2_pin7[0]), .pin3(_74193_2_pin7[1]), .pin4(_74193_2_pin7[2]),
    .pin5(_74193_2_pin7[3]), .pin6(_74193_1_pin7[0]), .pin7(_74193_1_pin7[1]), .pin8(_74193_1_pin7[2]),
    .pin9(_74193_1_pin7[3]), .pin10(1'b0), .pin11(Clock), .pin12(Addr15), .pin13(Addr14), .pin14(Addr13),
    .pin15(Addr12), .pin16(Addr11), .pin17(Addr10), .pin18(Addr9), .pin19(Addr8), .pin20(1'b1));
  _74574 _74574_2 (
    .pin1(nAssertBus), .pin2(_74193_2_pin7[0]), .pin3(_74193_2_pin7[1]), .pin4(_74193_2_pin7[2]),
    .pin5(_74193_2_pin7[3]), .pin6(_74193_1_pin7[0]), .pin7(_74193_1_pin7[1]), .pin8(_74193_1_pin7[2]),
    .pin9(_74193_1_pin7[3]), .pin10(1'b0), .pin11(Clock), .pin12(Bus15), .pin13(Bus14), .pin14(Bus13),
    .pin15(Bus12), .pin16(Bus11), .pin17(Bus10), .pin18(Bus9), .pin19(Bus8), .pin20(1'b1));
  _74193 _74193_3 (
    .pin1(Bus[5]), .pin2(_74193_3_pin7[1]), .pin3(_74193_3_pin7[0]), .pin4(_74193_3_pin4),
    .pin5(_74193_3_pin5), .pin6(_74193_3_pin7[2]), .pin7(_74193_3_pin7[3]), .pin8(1'b0), .pin9(Bus[7]),
    .pin10(Bus[6]), .pin11(nLoad), .pin12(_74193_2_pin5), .pin13(_74193_2_pin4), .pin14(Clear),
    .pin15(Bus[4]), .pin16(1'b1));
  _74193 _74193_4 (
    .pin1(Bus[1]), .pin2(_74193_4_pin7[1]), .pin3(_74193_4_pin7[0]), .pin4(Dec), .pin5(Inc),
    .pin6(_74193_4_pin7[2]), .pin7(_74193_4_pin7[3]), .pin8(1'b0), .pin9(Bus[3]), .pin10(Bus[2]),
    .pin11(nLoad), .pin12(_74193_3_pin5), .pin13(_74193_3_pin4), .pin14(Clear), .pin15(Bus[0]), .pin16(1'b1));
  _74574 _74574_3 (
    .pin1(nAssertAddr), .pin2(_74193_4_pin7[0]), .pin3(_74193_4_pin7[1]), .pin4(_74193_4_pin7[2]),
    .pin5(_74193_4_pin7[3]), .pin6(_74193_3_pin7[0]), .pin7(_74193_3_pin7[1]), .pin8(_74193_3_pin7[2]),
    .pin9(_74193_3_pin7[3]), .pin10(1'b0), .pin11(Clock), .pin12(Addr7), .pin13(Addr6), .pin14(Addr5),
    .pin15(Addr4), .pin16(Addr3), .pin17(Addr2), .pin18(Addr1), .pin19(Addr0), .pin20(1'b1));
  _74574 _74574_4 (
    .pin1(nAssertBus), .pin2(_74193_4_pin7[0]), .pin3(_74193_4_pin7[1]), .pin4(_74193_4_pin7[2]),
    .pin5(_74193_4_pin7[3]), .pin6(_74193_3_pin7[0]), .pin7(_74193_3_pin7[1]), .pin8(_74193_3_pin7[2]),
    .pin9(_74193_3_pin7[3]), .pin10(1'b0), .pin11(Clock), .pin12(Bus7), .pin13(Bus6), .pin14(Bus5),
    .pin15(Bus4), .pin16(Bus3), .pin17(Bus2), .pin18(Bus1), .pin19(Bus0), .pin20(1'b1));

  // Notes on the sheet:
  //   nAssertAddr: default 1
  //   nAssertBus: default 1
  //   nLoad: default 1
  //   Inc: default 1
  //   Dec: default 1
endmodule
