// Digital circuit reg-16bit-xfer.dig as structural Verilog
module reg_16bit_xfer (
  input  Clock,
  input  [7:0] Bus__Main,
  input  [15:0] Bus__Xfer,
  input  [15:0] Bus__Addr,
  input  nAssertMainBusLow,
  input  nAssertMainBusHigh,
  input  nAssertXferBus,
  input  nAssertAddrBus,
  input  nLoadMainBusLow,
  input  nLoadMainBusHigh,
  input  nLoadXferBus,
  output [15:0] Register__Value
);

  wire Addr0, Addr1, Addr2, Addr3, Addr4, Addr5, Addr6, Addr7, Addr8, Addr9, Addr10, Addr11, Addr12, Addr13,
       Addr14, Addr15, and_1_out, and_2_out, and_3_out, and_4_out;
  wire [3:0] _74157_1_pin4, _74157_2_pin4, _74157_3_pin4, _74157_4_pin4;

  BusSplitter #(.Bits(16)) bussplitter_1 (
    .D(Bus__Addr), .OE(nAssertAddrBus), .D0(Addr0), .D1(Addr1), .D2(Addr2), .D3(Addr3), .D4(Addr4),
    .D5(Addr5), .D6(Addr6), .D7(Addr7), .D8(Addr8), .D9(Addr9), .D10(Addr10), .D11(Addr11), .D12(Addr12),
    .D13(Addr13), .D14(Addr14), .D15(Addr15));
  and and_1 (and_1_out, nLoadMainBusLow, nLoadMainBusLow);
  and and_2 (and_2_out, nLoadMainBusHigh, nLoadMainBusHigh);
  _74157 _74157_1 (
    .pin1(and_1_out), .pin2(Bus__Main[0]), .pin3(Bus__Xfer[0]), .pin4(_74157_1_pin4[0]), .pin5(Bus__Main[1]),
    .pin6(Bus__Xfer[1]), .pin7(_74157_1_pin4[1]), .pin8(1'b0), .pin9(_74157_1_pin4[2]), .pin10(Bus__Xfer[2]),
    .pin11(Bus__Main[2]), .pin12(_74157_1_pin4[3]), .pin13(Bus__Xfer[3]), .pin14(Bus__Main[3]), .pin15(1'b0),
    .pin16(1'b1));
  _74157 _74157_2 (
    .pin1(and_2_out), .pin2(Bus__Main[0]), .pin3(Bus__Xfer[8]), .pin4(_74157_2_pin4[0]), .pin5(Bus__Main[1]),
    .pin6(Bus__Xfer[9]), .pin7(_74157_2_pin4[1]), .pin8(1'b0), .pin9(_74157_2_pin4[2]),
    .pin10(Bus__Xfer[10]), .pin11(Bus__Main[2]), .pin12(_74157_2_pin4[3]), .pin13(Bus__Xfer[11]),
    .pin14(Bus__Main[3]), .pin15(1'b0), .pin16(1'b1));
  _74157 _74157_3 (
    .pin1(and_1_out), .pin2(Bus__Main[4]), .pin3(Bus__Xfer[4]), .pin4(_74157_3_pin4[0]), .pin5(Bus__Main[5]),
    .pin6(Bus__Xfer[5]), .pin7(_74157_3_pin4[1]), .pin8(1'b0), .pin9(_74157_3_pin4[2]), .pin10(Bus__Xfer[6]),
    .pin11(Bus__Main[6]), .pin12(_74157_3_pin4[3]), .pin13(Bus__Xfer[7]), .pin14(Bus__Main[7]), .pin15(1'b0),
    .pin16(1'b1));
  _74157 _74157_4 (
    .pin1(and_2_out), .pin2(Bus__Main[4]), .pin3(Bus__Xfer[12]), .pin4(_74157_4_pin4[0]),
    .pin5(Bus__Main[5]), .pin6(Bus__Xfer[13]), .pin7(_74157_4_pin4[1]), .pin8(1'b0), .pin9(_74157_4_pin4[2]),
    .pin10(Bus__Xfer[14]), .pin11(Bus__Main[6]), .pin12(_74157_4_pin4[3]), .pin13(Bus__Xfer[15]),
    .pin14(Bus__Main[7]), .pin15(1'b0), .pin16(1'b1));
  and and_3 (and_3_out, nLoadMainBusLow, nLoadXferBus);
  and and_4 (and_4_out, nLoadXferBus, nLoadMainBusHigh);
  _74574 _74574_1 (
    .pin1(1'b0), .pin2(_74157_3_pin4[3]), .pin3(_74157_3_pin4[2]), .pin4(_74157_3_pin4[1]),
    .pin5(_74157_3_pin4[0]), .pin6(_74157_1_pin4[3]), .pin7(_74157_1_pin4[2]), .pin8(_74157_1_pin4[1]),
    .pin9(_74157_1_pin4[0]), .pin10(1'b0), .pin11(and_3_out), .pin12(Register__Value[0]),
    .pin13(Register__Value[1]), .pin14(Register__Value[2]), .pin15(Register__Value[3]),
    .pin16(Register__Value[4]), .pin17(Register__Value[5]), .pin18(Register__Value[6]),
    .pin19(Register__Value[7]), .pin20(1'b1));
  _74574 _74574_2 (
    .pin1(1'b0), .pin2(_74157_4_pin4[3]), .pin3(_74157_4_pin4[2]), .pin4(_74157_4_pin4[1]),
    .pin5(_74157_4_pin4[0]), .pin6(_74157_2_pin4[3]), .pin7(_74157_2_pin4[2]), .pin8(_74157_2_pin4[1]),
    .pin9(_74157_2_pin4[0]), .pin10(1'b0), .pin11(and_4_out), .pin12(Register__Value[8]),
    .pin13(Register__Value[9]), .pin14(Register__Value[10]), .pin15(Register__Value[11]),
    .pin16(Register__Value[12]), .pin17(Register__Value[13]), .pin18(Register__Value[14]),
    .pin19(Register__Value[15]), .pin20(1'b1));
  _74541 _74541_1 (
    .pin1(nAssertMainBusLow), .pin2(Register__Value[7]), .pin3(Register__Value[6]),
    .pin4(Register__Value[5]), .pin5(Register__Value[4]), .pin6(Register__Value[3]),
    .pin7(Register__Value[2]), .pin8(Register__Value[1]), .pin9(Register__Value[0]), .pin10(1'b0),
    .pin11(Bus__Main[0]), .pin12(Bus__Main[1]), .pin13(Bus__Main[2]), .pin14(Bus__Main[3]),
    .pin15(Bus__Main[4]), .pin16(Bus__Main[5]), .pin17(Bus__Main[6]), .pin18(Bus__Main[7]), .pin19(1'b0),
    .pin20(1'b1));
  _74541 _74541_2 (
    .pin1(nAssertMainBusHigh), .pin2(Register__Value[15]), .pin3(Register__Value[14]),
    .pin4(Register__Value[13]), .pin5(Register__Value[12]), .pin6(Register__Value[11]),
    .pin7(Register__Value[10]), .pin8(Register__Value[9]), .pin9(Register__Value[8]), .pin10(1'b0),
    .pin11(Bus__Main[0]), .pin12(Bus__Main[1]), .pin13(Bus__Main[2]), .pin14(Bus__Main[3]),
    .pin15(Bus__Main[4]), .pin16(Bus__Main[5]), .pin17(Bus__Main[6]), .pin18(Bus__Main[7]), .pin19(1'b0),
    .pin20(1'b1));
  _74541 _74541_3 (
    .pin1(nAssertXferBus), .pin2(Register__Value[7]), .pin3(Register__Value[6]), .pin4(Register__Value[5]),
    .pin5(Register__Value[4]), .pin6(Register__Value[3]), .pin7(Register__Value[2]),
    .pin8(Register__Value[1]), .pin9(Register__Value[0]), .pin10(1'b0), .pin11(Bus__Xfer[0]),
    .pin12(Bus__Xfer[1]), .pin13(Bus__Xfer[2]), .pin14(Bus__Xfer[3]), .pin15(Bus__Xfer[4]),
    .pin16(Bus__Xfer[5]), .pin17(Bus__Xfer[6]), .pin18(Bus__Xfer[7]), .pin19(1'b0), .pin20(1'b1));
  _74541 _74541_4 (
    .pin1(nAssertXferBus), .pin2(Register__Value[15]), .pin3(Register__Value[14]),
    .pin4(Register__Value[13]), .pin5(Register__Value[12]), .pin6(Register__Value[11]),
    .pin7(Register__Value[10]), .pin8(Register__Value[9]), .pin9(Register__Value[8]), .pin10(1'b0),
    .pin11(Bus__Xfer[8]), .pin12(Bus__Xfer[9]), .pin13(Bus__Xfer[10]), .pin14(Bus__Xfer[11]),
    .pin15(Bus__Xfer[12]), .pin16(Bus__Xfer[13]), .pin17(Bus__Xfer[14]), .pin18(Bus__Xfer[15]), .pin19(1'b0),
    .pin20(1'b1));
  _74541 _74541_5 (
    .pin1(nAssertAddrBus), .pin2(Register__Value[7]), .pin3(Register__Value[6]), .pin4(Register__Value[5]),
    .pin5(Register__Value[4]), .pin6(Register__Value[3]), .pin7(Register__Value[2]),
    .pin8(Register__Value[1]), .pin9(Register__Value[0]), .pin10(1'b0), .pin11(Bus__Addr[0]),
    .pin12(Bus__Addr[1]), .pin13(Bus__Addr[2]), .pin14(Bus__Addr[3]), .pin15(Bus__Addr[4]),
    .pin16(Bus__Addr[5]), .pin17(Bus__Addr[6]), .pin18(Bus__Addr[7]), .pin19(1'b0), .pin20(1'b1));
  _74541 _74541_6 (
    .pin1(nAssertAddrBus), .pin2(Register__Value[15]), .pin3(Register__Value[14]),
    .pin4(Register__Value[13]), .pin5(Register__Value[12]), .pin6(Register__Value[11]),
    .pin7(Register__Value[10]), .pin8(Register__Value[9]), .pin9(Register__Value[8]), .pin10(1'b0),
    .pin11(Bus__Addr[8]), .pin12(Bus__Addr[9]), .pin13(Bus__Addr[10]), .pin14(Bus__Addr[11]),
    .pin15(Bus__Addr[12]), .pin16(Bus__Addr[13]), .pin17(Bus__Addr[14]), .pin18(Bus__Addr[15]), .pin19(1'b0),
    .pin20(1'b1));

  // Other names for the same wires on the sheet: Main7 = Bus__Main[7]; Main6 = Bus__Main[6]; Main5 = Bus__Main[5];
  //   Main4 = Bus__Main[4]; Main3 = Bus__Main[3]; Main2 = Bus__Main[2]; Main1 = Bus__Main[1]; Main0 = Bus__Main[0];
  //   Bus3 = Bus__Xfer[3]; Bus2 = Bus__Xfer[2]; Bus1 = Bus__Xfer[1]; Bus0 = Bus__Xfer[0]; Bus15 = Bus__Xfer[15];
  //   Bus14 = Bus__Xfer[14]; Bus13 = Bus__Xfer[13]; Bus12 = Bus__Xfer[12]; Bus11 = Bus__Xfer[11];
  //   Bus10 = Bus__Xfer[10]; Bus9 = Bus__Xfer[9]; Bus8 = Bus__Xfer[8]; Bus4 = Bus__Xfer[4]; Bus5 = Bus__Xfer[5];
  //   Bus6 = Bus__Xfer[6]; Bus7 = Bus__Xfer[7]

  // Notes on the sheet:
  //   nAssertMainBusLow: default 1
  //   nAssertMainBusHigh: default 1
  //   nAssertXferBus: default 1
  //   nAssertAddrBus: default 1
  //   nLoadMainBusLow: default 1
  //   nLoadMainBusHigh: default 1
  //   nLoadXferBus: default 1
endmodule
