// Digital circuit reg-constant.dig as structural Verilog
module reg_constant (
  input  [7:0] MEMDATAIn,
  input  Reg__Assert,
  input  Reg__Load,
  output [7:0] MainBusOut
);

  wire nand_1_out, nand_3_out, nand_4_out, Reg__Valid;

  _74574 _8bit_GPR (
    .pin1(Reg__Assert), .pin2(MEMDATAIn[7]), .pin3(MEMDATAIn[6]), .pin4(MEMDATAIn[5]), .pin5(MEMDATAIn[4]),
    .pin6(MEMDATAIn[3]), .pin7(MEMDATAIn[2]), .pin8(MEMDATAIn[1]), .pin9(MEMDATAIn[0]), .pin10(1'b0),
    .pin11(Reg__Load), .pin12(MainBusOut[0]), .pin13(MainBusOut[1]), .pin14(MainBusOut[2]),
    .pin15(MainBusOut[3]), .pin16(MainBusOut[4]), .pin17(MainBusOut[5]), .pin18(MainBusOut[6]),
    .pin19(MainBusOut[7]), .pin20(1'b1));
  nand nand_1 (nand_1_out, Reg__Load, nand_4_out);
  nand nand_2 (Reg__Valid, nand_3_out, nand_3_out);
  nand nand_3 (nand_3_out, Reg__Assert, nand_4_out);
  nand nand_4 (nand_4_out, nand_1_out, Reg__Assert);

  // Notes on the sheet:
  //   MEMDATAIn: default 105
  //   Reg__Assert: default 1
  //   Reg__Load: default 1
  //   Leaving this on for now, but I think this is 
  //   only used for driving the LEDs?
endmodule
