// Digital circuit pipeline-stage0.dig as structural Verilog
module pipeline_stage0 (
  input  [7:0] MEMDATA,
  input  BusRequest,
  input  FetchSuppress,
  input  Flags__5__PCRA__Flip,
  input  ClockIn,
  output Pipe0Out__0__IncPCRA0,
  output Pipe0Out__1__IncPCRA1,
  output [7:0] Pipe0Out
);

  wire _7404_1_pin2, _7404_1_pin11, PIPELATCH0, PIPELATCH1, PIPELATCH2, PIPELATCH3, PIPELATCH4, PIPELATCH5,
       PIPELATCH6, PIPELATCH7;

  _74574 _74574_1 (
    .pin1(1'b0), .pin2(MEMDATA[7]), .pin3(MEMDATA[6]), .pin4(MEMDATA[5]), .pin5(MEMDATA[4]),
    .pin6(MEMDATA[3]), .pin7(MEMDATA[2]), .pin8(MEMDATA[1]), .pin9(MEMDATA[0]), .pin10(1'b0),
    .pin11(ClockIn), .pin12(PIPELATCH0), .pin13(PIPELATCH1), .pin14(PIPELATCH2), .pin15(PIPELATCH3),
    .pin16(PIPELATCH4), .pin17(PIPELATCH5), .pin18(PIPELATCH6), .pin19(PIPELATCH7), .pin20(1'b1));
  _7404 _7404_1 (
    .pin1(Flags__5__PCRA__Flip), .pin2(_7404_1_pin2), .pin3(_7404_1_pin2), .pin4(Pipe0Out__0__IncPCRA0),
    .pin5(1'b0), .pin7(1'b0), .pin9(1'b0), .pin10(Pipe0Out__1__IncPCRA1), .pin11(_7404_1_pin11),
    .pin12(_7404_1_pin11), .pin13(BusRequest), .pin14(1'b1));  // open: pin6, pin8
  _74153 _74153_1 (
    .pin1(1'b0), .pin2(FetchSuppress), .pin3(PIPELATCH0), .pin4(1'b0), .pin5(1'b0), .pin6(MEMDATA[0]),
    .pin7(Pipe0Out[0]), .pin8(1'b0), .pin9(Pipe0Out[1]), .pin10(MEMDATA[1]), .pin11(1'b0), .pin12(1'b0),
    .pin13(PIPELATCH1), .pin14(BusRequest), .pin15(1'b0), .pin16(1'b1));
  _74153 _74153_2 (
    .pin1(1'b0), .pin2(FetchSuppress), .pin3(PIPELATCH4), .pin4(1'b0), .pin5(1'b0), .pin6(MEMDATA[4]),
    .pin7(Pipe0Out[4]), .pin8(1'b0), .pin9(Pipe0Out[5]), .pin10(MEMDATA[5]), .pin11(1'b0), .pin12(1'b0),
    .pin13(PIPELATCH5), .pin14(BusRequest), .pin15(1'b0), .pin16(1'b1));
  _74153 _74153_3 (
    .pin1(1'b0), .pin2(FetchSuppress), .pin3(PIPELATCH2), .pin4(1'b0), .pin5(1'b0), .pin6(MEMDATA[2]),
    .pin7(Pipe0Out[2]), .pin8(1'b0), .pin9(Pipe0Out[3]), .pin10(MEMDATA[3]), .pin11(1'b0), .pin12(1'b0),
    .pin13(PIPELATCH3), .pin14(BusRequest), .pin15(1'b0), .pin16(1'b1));
  _74153 _74153_4 (
    .pin1(1'b0), .pin2(FetchSuppress), .pin3(PIPELATCH6), .pin4(1'b0), .pin5(1'b0), .pin6(MEMDATA[6]),
    .pin7(Pipe0Out[6]), .pin8(1'b0), .pin9(Pipe0Out[7]), .pin10(MEMDATA[7]), .pin11(1'b0), .pin12(1'b0),
    .pin13(PIPELATCH7), .pin14(BusRequest), .pin15(1'b0), .pin16(1'b1));

  // Other names for the same wires on the sheet: PipeOut0 = Pipe0Out[0]; PipeOut1 = Pipe0Out[1];
  //   PipeOut2 = Pipe0Out[2]; PipeOut3 = Pipe0Out[3]; PipeOut4 = Pipe0Out[4]; PipeOut5 = Pipe0Out[5];
  //   PipeOut6 = Pipe0Out[6]; PipeOut7 = Pipe0Out[7]
endmodule

/* Test case Basic Tests:
BusRequest FetchSuppress ClockIn MEMDATA Pipe0Out Pipe0Out\_0\_IncPCRA0 Pipe0Out\_1\_IncPCRA1
# test normal MEMDATA->Pipe0Out
1	   1             1       x       x        x                     x
1	   1             0       1       x        x                     x
1          1             1       1       1        x                     1
1          1             0       0       1        x                     x
1          1             1       0       0        x                     1

# test fetch suppress
   # setup
1          1             0       2       x        x                     x
1          1             1       2       2        x                     x
   # pull fetch suppress low, pipeout is DC till clock rises
1          0             0       3       x        x                     x
1          0             1       3       0        x                     x
*/
