// Digital circuit pipeline-stage1.dig as structural Verilog
module pipeline_stage1 (
  input  ClockIn,
  input  BusRequest,
  input  Flags__0__Overflow,
  input  Flags__1__Sign,
  input  Flags__2__Zero,
  input  Flags__3__CarryA,
  input  Flags__4__CarryL,
  input  Flags__5__PCRA__Flip,
  input  Flags__6__Reset,
  input  [7:0] PipeIn,
  output [7:0] PipeOut,
  output Pipe1Out__0__LHS0,
  output Pipe1Out__1__LHS1,
  output Pipe1Out__2__RHS0,
  output Pipe1Out__3__RHS1,
  output Pipe1Out__4__ALUOP0,
  output Pipe1Out__5__ALUOP1,
  output Pipe1Out__6__ALUOP2,
  output Pipe1Out__7__ALUOP3,
  output Pipe1Out__8__XLD0,
  output Pipe1Out__9__XLD1,
  output Pipe1Out__10__XLD2,
  output Pipe1Out__11__XLD3,
  output Pipe1Out__12__XA0,
  output Pipe1Out__13__XA1,
  output Pipe1Out__14__XA2,
  output Pipe1Out__15__FetchSuppress
);

  wire Clock, nand_1_out, not_1_out;
  wire [7:0] _74574_1_pin12, _74574_2_pin9, _74574_3_pin9;

  not not_1 (not_1_out, ClockIn);
  not not_2 (Clock, not_1_out);
  pipeline_stage1_rom1 pipeline_stage1_rom1_1 (
    .nCE(1'b0), .nOE(1'b0), .nWE(1'b1), .VCC(1'b1), .GND(1'b0), .I_O0(_74574_2_pin9[7]),
    .I_O1(_74574_2_pin9[6]), .I_O2(_74574_2_pin9[5]), .I_O3(_74574_2_pin9[4]), .I_O4(_74574_2_pin9[3]),
    .I_O5(_74574_2_pin9[2]), .I_O6(_74574_2_pin9[1]), .I_O7(_74574_2_pin9[0]), .A0(PipeIn[0]),
    .A1(PipeIn[1]), .A2(PipeIn[2]), .A3(PipeIn[3]), .A4(PipeIn[4]), .A5(PipeIn[5]), .A6(PipeIn[6]),
    .A7(PipeIn[7]), .A8(Flags__0__Overflow), .A9(Flags__1__Sign), .A10(Flags__2__Zero),
    .A11(Flags__3__CarryA), .A12(Flags__4__CarryL), .A13(Flags__5__PCRA__Flip), .A14(Flags__6__Reset));
  pipeline_stage1_rom2 pipeline_stage1_rom2_1 (
    .nCE(1'b0), .nOE(1'b0), .nWE(1'b1), .VCC(1'b1), .GND(1'b0), .I_O0(_74574_3_pin9[7]),
    .I_O1(_74574_3_pin9[6]), .I_O2(_74574_3_pin9[5]), .I_O3(_74574_3_pin9[4]), .I_O4(_74574_3_pin9[3]),
    .I_O5(_74574_3_pin9[2]), .I_O6(_74574_3_pin9[1]), .I_O7(_74574_3_pin9[0]), .A0(PipeIn[0]),
    .A1(PipeIn[1]), .A2(PipeIn[2]), .A3(PipeIn[3]), .A4(PipeIn[4]), .A5(PipeIn[5]), .A6(PipeIn[6]),
    .A7(PipeIn[7]), .A8(Flags__0__Overflow), .A9(Flags__1__Sign), .A10(Flags__2__Zero),
    .A11(Flags__3__CarryA), .A12(Flags__4__CarryL), .A13(Flags__5__PCRA__Flip), .A14(Flags__6__Reset));
  _74574 _74574_1 (
    .pin1(1'b0), .pin2(PipeIn[7]), .pin3(PipeIn[6]), .pin4(PipeIn[5]), .pin5(PipeIn[4]), .pin6(PipeIn[3]),
    .pin7(PipeIn[2]), .pin8(PipeIn[1]), .pin9(PipeIn[0]), .pin10(1'b0), .pin11(Clock),
    .pin12(_74574_1_pin12[0]), .pin13(_74574_1_pin12[1]), .pin14(_74574_1_pin12[2]),
    .pin15(_74574_1_pin12[3]), .pin16(_74574_1_pin12[4]), .pin17(_74574_1_pin12[5]),
    .pin18(_74574_1_pin12[6]), .pin19(_74574_1_pin12[7]), .pin20(1'b1));
  nand nand_1 (nand_1_out, Pipe1Out__15__FetchSuppress, BusRequest);
  and and_1 (PipeOut[0], _74574_1_pin12[0], nand_1_out);
  and and_2 (PipeOut[1], _74574_1_pin12[1], nand_1_out);
  and and_3 (PipeOut[2], _74574_1_pin12[2], nand_1_out);
  and and_4 (PipeOut[3], _74574_1_pin12[3], nand_1_out);
  and and_5 (PipeOut[4], _74574_1_pin12[4], nand_1_out);
  and and_6 (PipeOut[5], _74574_1_pin12[5], nand_1_out);
  and and_7 (PipeOut[6], _74574_1_pin12[6], nand_1_out);
  and and_8 (PipeOut[7], _74574_1_pin12[7], nand_1_out);
  _74574 _74574_2 (
    .pin1(1'b0), .pin2(_74574_2_pin9[0]), .pin3(_74574_2_pin9[1]), .pin4(_74574_2_pin9[2]),
    .pin5(_74574_2_pin9[3]), .pin6(_74574_2_pin9[4]), .pin7(_74574_2_pin9[5]), .pin8(_74574_2_pin9[6]),
    .pin9(_74574_2_pin9[7]), .pin10(1'b0), .pin11(Clock), .pin12(Pipe1Out__0__LHS0),
    .pin13(Pipe1Out__1__LHS1), .pin14(Pipe1Out__2__RHS0), .pin15(Pipe1Out__3__RHS1),
    .pin16(Pipe1Out__4__ALUOP0), .pin17(Pipe1Out__5__ALUOP1), .pin18(Pipe1Out__6__ALUOP2),
    .pin19(Pipe1Out__7__ALUOP3), .pin20(1'b1));
  _74574 _74574_3 (
    .pin1(1'b0), .pin2(_74574_3_pin9[0]), .pin3(_74574_3_pin9[1]), .pin4(_74574_3_pin9[2]),
    .pin5(_74574_3_pin9[3]), .pin6(_74574_3_pin9[4]), .pin7(_74574_3_pin9[5]), .pin8(_74574_3_pin9[6]),
    .pin9(_74574_3_pin9[7]), .pin10(1'b0), .pin11(Clock), .pin12(Pipe1Out__8__XLD0),
    .pin13(Pipe1Out__9__XLD1), .pin14(Pipe1Out__10__XLD2), .pin15(Pipe1Out__11__XLD3),
    .pin16(Pipe1Out__12__XA0), .pin17(Pipe1Out__13__XA1), .pin18(Pipe1Out__14__XA2),
    .pin19(Pipe1Out__15__FetchSuppress), .pin20(1'b1));

  // Notes on the sheet:
  //   This technique is unlikely to work in verilog.
  //   Will likely need to use a higher clock and a "half-clock" signal
endmodule
