// Digital circuit pipeline-stage2-rom2.dig as structural Verilog
// 256K (32K x 8) Paged Parallel EEPROM;
// DATA Polling for End of Write Detection not implemented!
module pipeline_stage2_rom2 (
  input  nCE,
  input  nOE,
  input  nWE,
  input  VCC,
  input  GND,
  input  I_O0,
  input  I_O1,
  input  I_O2,
  input  I_O3,
  input  I_O4,
  input  I_O5,
  input  I_O6,
  input  I_O7,
  input  A0,
  input  A1,
  input  A2,
  input  A3,
  input  A4,
  input  A5,
  input  A6,
  input  A7,
  input  A8,
  input  A9,
  input  A10,
  input  A11,
  input  A12,
  input  A13,
  input  A14
);

  wire nor_1_out;
  wire [7:0] Stage1__ROM2_d;

  EEPROM #(.AddrBits(15), .isProgramMemory("true"), .Bits(8)) Stage1__ROM2 (
    .A({A14, A13, A12, A11, A10, A9, A8, A7, A6, A5, A4, A3, A2, A1, A0}), .CS(~nCE), .WE(~nWE), .OE(~nOE),
    .D(Stage1__ROM2_d));
  nor nor_1 (nor_1_out, nCE, ~nWE, nOE);  // NOr
  PowerSupply powersupply_1 (.VDD(VCC), .GND(GND));
  BusSplitter #(.Bits(8)) bussplitter_1 (
    .D(Stage1__ROM2_d), .OE(nor_1_out), .D0(I_O0), .D1(I_O1), .D2(I_O2), .D3(I_O3), .D4(I_O4), .D5(I_O5),
    .D6(I_O6), .D7(I_O7));

  // Notes on the sheet:
  //   nCE: pin 20, default 1
  //   nOE: pin 22, default 1
  //   nWE: pin 27, default 1
  //   VCC: pin 28, default 1
  //   GND: pin 14
  //   I_O0: pin 11
  //   I_O1: pin 12
  //   I_O2: pin 13
  //   I_O3: pin 15
  //   I_O4: pin 16
  //   I_O5: pin 17
  //   I_O6: pin 18
  //   I_O7: pin 19
  //   A0: pin 10
  //   A1: pin 9
  //   A2: pin 8
  //   A3: pin 7
  //   A4: pin 6
  //   A5: pin 5
  //   A6: pin 4
  //   A7: pin 3
  //   A8: pin 25
  //   A9: pin 24
  //   A10: pin 21
  //   A11: pin 23
  //   A12: pin 2
  //   A13: pin 26
  //   A14: pin 1
  //   contents of Stage1__ROM2 (hex, n*v repeats v):
  //   4,4,4,4,4,4,4,4,4,4,4,4,4,4,4,4,4,4,4,4,4,4,4,4,4,4,4,4,4,4,4,4,4,4,4,4,4,4,4,4,4,
  //   4,4,4,4,4,4,4,4,4,4,4,5,6,7,4,4,4,4,4,4,4,4,4,30,30,30,30,34,34,34,34,38,38,38,38,
  //   30,30,30,30,34,34,34,34,38,38,38,38,4,4,4,4,48,48,48,24,4,4,4,4,4,4,4,4,4,4,4,4,4,
  //   4,4,4,4,4,2c,2c,2c,2c,2c,2c,2d,2d,2d,2d,2d,2d,4,4,4,4,4,4,4,4,4,4,4,4,4,4,4,4,4,4,
  //   4,4,4,4,4,4,4,4,4,4,4,4,4,4,4,4,4,4,4,4,4,4,4,4,4,4,4,4,4,4,4,4,4,4,4,4,4,4,4,4,4,
  //   4,4,4,4,4,4,4,4,4,4,4,4,4,4,4,4,4,4,4,4,4,4,4,4,4,4,4,4,4,4,4,4,4,4,4,4,4,4,4,4,4,
  //   4,4,4,4,4,4,4,4,4,4,4,4,4,4,4,4,4,4,4,4,4,4,4,4,4,4,4,4,4,4,4,4,4,4,4,4,4,4,4,4,4,
  //   4,4,4,4,4,4,4,4,4,4,4,4,4,4,4,4,4,4,4,4,4,4,4,4,4,4,4,4,4,4,4,4,4,4,4,4,4,4,4,4,4,
  //   5,6,7,4,4,4,4,4,4,4,4,4,30,30,30,30,34,34,34,34,38,38,38,38,30,30,30,30,34,34,34,
  //   34,38,38,38,38,4,4,4,4,48,48,48,24,4,4,4,4,4,4,4,4,4,4,4,4,4,4,4,4,4,4,2c,2c,2c,2c,
  //   2c,2c,2d,2d,2d,2d,2d,2d,4,4,4,4,4,4,4,4,4,4,4,4,4,4,4,4,4,4,4,4,4,4,4,4,4,4,4,4,4,
  //   4,4,4,4,4,4,4,4,4,4,4,4,4,4,4,4,4,4,4,4,4,4,4,4,4,4,4,4,4,4,4,4,4,4,4,4,4,4,4,4,4,
  //   4,4,4,4,4,4,4,4,4,4,4,4,4,4,4,4,4,4,4,4,4,4,4,4,4,4,4,4,4,4,4,4,4,4,4,4,4,4,4,4,4,
  //   4,4,4,4,4,4,4,4,4,4,4,4,4,4,4,4,4,4,4,4,4,4,4,4,4,4,4,4,4,4,4,4,4,4,4,4,4,4,4,4,4,
  //   4,4,4,4,4,4,4,4,4,4,4,4,4,4,4,4,4,4,4,4,4,4,4,4,4,4,4,4,4,4,5,6,7,4,4,4,4,4,4,4,4,
  //   4,30,30,30,30,34,34,34,34,38,38,38,38,30,30,30,30,34,34,34,34,38,38,38,38,4,4,4,4,
  //   48,48,48,24,4,4,4,4,4,4,4,4,4,4,4,4,4,4,4,4,4,4,2c,2c,2c,2c,2c,2c,2d,2d,2d,2d,2d,
  //   2d,4,4,4,4,4,4,4,4,4,4,4,4,4,4,4,4,4,4,4,4,4,4,4,4,4,4,4,4,4,4,4,4,4,4,4,4,4,4,4,
  //   4,4,4,4,4,4,4,4,4,4,4,4,4,4,4,4,4,4,4,4,4,4,4,4,4,4,4,4,4,4,4,4,4,4,4,4,4,4,4,4,4,
  //   4,4,4,4,4,4,4,4,4,4,4,4,4,4,4,4,4,4,4,4,4,4,4,4,4,4,4,4,4,4,4,4,4,4,4,4,4,4,4,4,4,
  //   4,4,4,4,4,4,4,4,4,4,4,4,4,4,4,4,4,4,4,4,4,4,4,4,4,4,4,4,4,4,4,4,4,4,4,4,4,4,4,4,4,
  //   4,4,4,4,4,4,4,4,4,4,4,4,4,4,4,4,4,4,4,4,5,6,7,4,4,4,4,4,4,4,4,4,30,30,30,30,34,34,
  //   34,34,38,38,38,38,30,30,30,30,34,34,34,34,38,38,38,38,4,4,4,4,48,48,48,24,4,4,4,4,
  //   4,4,4,4,4,4,4,4,4,4,4,4,4,4,2c,2c,2c,2c,2c,2c,2d,2d,2d,2d,2d,2d,4,4,4,4,4,4,4,4,4,
  //   4,4,4,4,4,4,4,4,4,4,4,4,4,4,4,4,4,4,4,4,4,4,4,4,4,4,4,4,4,4,4,4,4,4,4,4,4,4,4,4,4,
  //   4,4,4,4,4,4,4,4,4,4,4,4,4,4,4,4,4,4,4,4,4,4,4,4,4,4,4,4,4,4,4,4,4,4,4,4,4,4,4,4,4,
  //   4,4,4,4,4,4,4,4,4,4,4,4,4,4,4,4,4,4,4,4,4,4,4,4,4,4,4,4,4,4,4,4,4,4,4,4,4,4,4,4,4,
  //   4,4,4,4,4,4,4,4,4,4,4,4,4,4,4,4,4,4,4,4,4,4,4,4,4,4,4,4,4,4,4,4,4,4,4,4,4,4,4,4,4,
  //   4,4,4,4,4,4,4,4,4,5,6,7,4,4,4,4,4,4,4,4,4,30,30,30,30,34,34,34,34,38,38,38,38,30,
  //   30,30,30,34,34,34,34,38,38,38,38,4,4,4,4,48,48,48,24,4,4,4,4,4,4,4,4,4,4,4,4,4,4,
  //   4,4,4,4,2c,2c,2c,2c,2c,2c,2d,2d,2d,2d,2d,2d,4,4,4,4,4,4,4,4,4,4,4,4,4,4,4,4,4,4,4,
  //   4,4,4,4,4,4,4,4,4,4,4,4,4,4,4,4,4,4,4,4,4,4,4,4,4,4,4,4,4,4,4,4,4,4,4,4,4,4,4,4,4,
  //   4,4,4,4,4,4,4,4,4,4,4,4,4,4,4,4,4,4,4,4,4,4,4,4,4,4,4,4,4,4,4,4,4,4,4,4,4,4,4,4,4,
  //   4,4,4,4,4,4,4,4,4,4,4,4,4,4,4,4,4,4,4,4,4,4,4,4,4,4,4,4,4,4,4,4,4,4,4,4,4,4,4,4,4,
  //   4,4,4,4,4,4,4,4,4,4,4,4,4,4,4,4,4,4,4,4,4,4,4,4,4,4,4,4,4,4,4,4,4,4,4,4,4,4,4,4,5,
  //   6,7,4,4,4,4,4,4,4,4,4,30,30,30,30,34,34,34,34,38,38,38,38,30,30,30,30,34,34,34,34,
  //   38,38,38,38,4,4,4,4,48,48,48,24,4,4,4,4,4,4,4,4,4,4,4,4,4,4,4,4,4,4,2c,2c,2c,2c,2c,
  //   2c,2d,2d,2d,2d,2d,2d,4,4,4,4,4,4,4,4,4,4,4,4,4,4,4,4,4,4,4,4,4,4,4,4,4,4,4,4,4,4,
  //   4,4,4,4,4,4,4,4,4,4,4,4,4,4,4,4,4,4,4,4,4,4,4,4,4,4,4,4,4,4,4,4,4,4,4,4,4,4,4,4,4,
  //   4,4,4,4,4,4,4,4,4,4,4,4,4,4,4,4,4,4,4,4,4,4,4,4,4,4,4,4,4,4,4,4,4,4,4,4,4,4,4,4,4,
  //   4,4,4,4,4,4,4,4,4,4,4,4,4,4,4,4,4,4,4,4,4,4,4,4,4,4,4,4,4,4,4,4,4,4,4,4,4,4,4,4,4,
  //   4,4,4,4,4,4,4,4,4,4,4,4,4,4,4,4,4,4,4,4,4,4,4,4,4,4,4,4,4,5,6,7,4,4,4,4,4,4,4,4,4,
  //   30,30,30,30,34,34,34,34,38,38,38,38,30,30,30,30,34,34,34,34,38,38,38,38,4,4,4,4,48,
  //   48,48,24,4,4,4,4,4,4,4,4,4,4,4,4,4,4,4,4,4,4,2c,2c,2c,2c,2c,2c,2d,2d,2d,2d,2d,2d,
  //   4,4,4,4,4,4,4,4,4,4,4,4,4,4,4,4,4,4,4,4,4,4,4,4,4,4,4,4,4,4,4,4,4,4,4,4,4,4,4,4,4,
  //   4,4,4,4,4,4,4,4,4,4,4,4,4,4,4,4,4,4,4,4,4,4,4,4,4,4,4,4,4,4,4,4,4,4,4,4,4,4,4,4,4,
  //   4,4,4,4,4,4,4,4,4,4,4,4,4,4,4,4,4,4,4,4,4,4,4,4,4,4,4,4,4,4,4,4,4,4,4,4,4,4,4,4,4,
  //   4,4,4,4,4,4,4,4,4,4,4,4,4,4,4,4,4,4,4,4,4,4,4,4,4,4,4,4,4,4,4,4,4,4,4,4,4,4,4,4,4,
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endmodule

/* Test case:
~CE ~WE ~OE A14 A13 A12 A11 A10 A9 A8 A7 A6 A5 A4 A3 A2 A1 A0 I/O7 I/O6 I/O5 I/O4 I/O3 I/O2 I/O1 I/O0 I/O7_out I/O6_out I/O5_out I/O4_out I/O3_out I/O2_out I/O1_out I/O0_out

let r = random(240) ;

loop (a,8)
  1   1  1  bits(15,a) bits(8,0) x x x x x x x x
  0   0  1  bits(15,a) bits(8,0) x x x x x x x x
  0   0  1  bits(15,a) bits(8,a+r) x x x x x x x x
  1   1  1  bits(15,a) bits(8,a+r) x x x x x x x x
end loop

loop (a,8)
  0   1  0  bits(15,a) z z z z z z z z bits(8,a+r)
end loop
*/
