// Digital circuit pipeline-stage2.dig as structural Verilog
module pipeline_stage2 (
  input  ClockIn,
  input  Flags__0__Overflow,
  input  Flags__1__Sign,
  input  Flags__2__Zero,
  input  Flags__3__CarryA,
  input  Flags__4__CarryL,
  input  Flags__5__PCRA__Flip,
  input  Flags__6__Reset,
  input  [7:0] PipeIn,
  output [7:0] PipeOut,
  output Pipe2Out__0__MainAssert0,
  output Pipe2Out__1__MainAssert1,
  output Pipe2Out__2__MainAssert2,
  output Pipe2Out__3__MainAssert3,
  output Pipe2Out__4__MainLoad0,
  output Pipe2Out__5__MainLoad1,
  output Pipe2Out__6__MainLoad2,
  output Pipe2Out__7__MainLoad3,
  output Pipe2Out__8__Inc0,
  output Pipe2Out__9__Inc1,
  output Pipe2Out__10__Addr0,
  output Pipe2Out__11__Addr1,
  output Pipe2Out__12__Addr2,
  output Pipe2Out__13__BusRequest,
  output Pipe2Out__14__PCRA__Flip,
  output Pipe2Out__15__Break
);

  wire Clock, not_1_out;
  wire [7:0] _74574_2_pin2, _74574_3_pin2;

  not not_1 (not_1_out, ClockIn);
  not not_2 (Clock, not_1_out);
  pipeline_stage2_rom1 pipeline_stage2_rom1_1 (
    .nCE(1'b0), .nOE(1'b0), .nWE(1'b1), .VCC(1'b1), .GND(1'b0), .I_O0(_74574_2_pin2[0]),
    .I_O1(_74574_2_pin2[1]), .I_O2(_74574_2_pin2[2]), .I_O3(_74574_2_pin2[3]), .I_O4(_74574_2_pin2[4]),
    .I_O5(_74574_2_pin2[5]), .I_O6(_74574_2_pin2[6]), .I_O7(_74574_2_pin2[7]), .A0(PipeIn[0]),
    .A1(PipeIn[1]), .A2(PipeIn[2]), .A3(PipeIn[3]), .A4(PipeIn[4]), .A5(PipeIn[5]), .A6(PipeIn[6]),
    .A7(PipeIn[7]), .A8(Flags__0__Overflow), .A9(Flags__1__Sign), .A10(Flags__2__Zero),
    .A11(Flags__3__CarryA), .A12(Flags__4__CarryL), .A13(Flags__5__PCRA__Flip), .A14(Flags__6__Reset));
  pipeline_stage2_rom2 pipeline_stage2_rom2_1 (
    .nCE(1'b0), .nOE(1'b0), .nWE(1'b1), .VCC(1'b1), .GND(1'b0), .I_O0(_74574_3_pin2[0]),
    .I_O1(_74574_3_pin2[1]), .I_O2(_74574_3_pin2[2]), .I_O3(_74574_3_pin2[3]), .I_O4(_74574_3_pin2[4]),
    .I_O5(_74574_3_pin2[5]), .I_O6(_74574_3_pin2[6]), .I_O7(_74574_3_pin2[7]), .A0(PipeIn[0]),
    .A1(PipeIn[1]), .A2(PipeIn[2]), .A3(PipeIn[3]), .A4(PipeIn[4]), .A5(PipeIn[5]), .A6(PipeIn[6]),
    .A7(PipeIn[7]), .A8(Flags__0__Overflow), .A9(Flags__1__Sign), .A10(Flags__2__Zero),
    .A11(Flags__3__CarryA), .A12(Flags__4__CarryL), .A13(Flags__5__PCRA__Flip), .A14(Flags__6__Reset));
  _74574 _74574_1 (
    .pin1(1'b0), .pin2(PipeIn[7]), .pin3(PipeIn[6]), .pin4(PipeIn[5]), .pin5(PipeIn[4]), .pin6(PipeIn[3]),
    .pin7(PipeIn[2]), .pin8(PipeIn[1]), .pin9(PipeIn[0]), .pin10(1'b0), .pin11(Clock), .pin12(PipeOut[0]),
    .pin13(PipeOut[1]), .pin14(PipeOut[2]), .pin15(PipeOut[3]), .pin16(PipeOut[4]), .pin17(PipeOut[5]),
    .pin18(PipeOut[6]), .pin19(PipeOut[7]), .pin20(1'b1));
  _74574 _74574_2 (
    .pin1(1'b0), .pin2(_74574_2_pin2[0]), .pin3(_74574_2_pin2[1]), .pin4(_74574_2_pin2[2]),
    .pin5(_74574_2_pin2[3]), .pin6(_74574_2_pin2[4]), .pin7(_74574_2_pin2[5]), .pin8(_74574_2_pin2[6]),
    .pin9(_74574_2_pin2[7]), .pin10(1'b0), .pin11(Clock), .pin12(Pipe2Out__0__MainAssert0),
    .pin13(Pipe2Out__1__MainAssert1), .pin14(Pipe2Out__2__MainAssert2), .pin15(Pipe2Out__3__MainAssert3),
    .pin16(Pipe2Out__4__MainLoad0), .pin17(Pipe2Out__5__MainLoad1), .pin18(Pipe2Out__6__MainLoad2),
    .pin19(Pipe2Out__7__MainLoad3), .pin20(1'b1));
  _74574 _74574_3 (
    .pin1(1'b0), .pin2(_74574_3_pin2[0]), .pin3(_74574_3_pin2[1]), .pin4(_74574_3_pin2[2]),
    .pin5(_74574_3_pin2[3]), .pin6(_74574_3_pin2[4]), .pin7(_74574_3_pin2[5]), .pin8(_74574_3_pin2[6]),
    .pin9(_74574_3_pin2[7]), .pin10(1'b0), .pin11(Clock), .pin12(Pipe2Out__8__Inc0),
    .pin13(Pipe2Out__9__Inc1), .pin14(Pipe2Out__10__Addr0), .pin15(Pipe2Out__11__Addr1),
    .pin16(Pipe2Out__12__Addr2), .pin17(Pipe2Out__13__BusRequest), .pin18(Pipe2Out__14__PCRA__Flip),
    .pin19(Pipe2Out__15__Break), .pin20(1'b1));

  // Notes on the sheet:
  //   This technique is unlikely to work in verilog.
  //   Will likely need to use a higher clock and a "half-clock" signal
endmodule
