// Digital circuit pipeline.dig as structural Verilog
module pipeline (
);

  pipeline_stage0 pipeline_stage0_1 ();  // open: MEMDATA, BusRequest, FetchSuppress, Flags__5__PCRA__Flip, ClockIn, Pipe0Out, Pipe0Out__0__IncPCRA0, Pipe0Out__1__IncPCRA1
  pipeline_stage1 pipeline_stage1_1 ();  // open: ClockIn, PipeIn, Flags__0__Overflow, Flags__1__Sign, Flags__2__Zero, Flags__3__CarryA, Flags__4__CarryL, Flags__5__PCRA__Flip, Flags__6__Reset, BusRequest, PipeOut
endmodule
